// Logisim project Circuit.circ as structural Verilog
module half_adder (
  input  A,
  input  B,
  output sum,
  output carry_out
);

  xor xor_1 (sum, A, B);
  and and_1 (carry_out, A, B);
endmodule

module full_adder (
  input  A,
  input  B,
  input  Cin,
  output Sum_out,
  output carry_out
);

  wire half_adder_1_carry_out, half_adder_1_sum, half_adder_2_carry_out;

  half_adder half_adder_1 (.A(A), .B(B), .sum(half_adder_1_sum), .carry_out(half_adder_1_carry_out));
  half_adder half_adder_2 (.A(half_adder_1_sum), .B(Cin), .sum(Sum_out), .carry_out(half_adder_2_carry_out));
  or or_1 (carry_out, half_adder_2_carry_out, half_adder_1_carry_out);
endmodule

module two_bit_adder (
  input  cin,
  input  [1:0] A,
  input  [1:0] B,
  output [1:0] sum_out,
  output carry_out
);

  wire full_adder_1_carry_out;

  full_adder full_adder_1 (.A(A[0]), .B(B[0]), .Cin(cin), .Sum_out(sum_out[0]), .carry_out(full_adder_1_carry_out));
  full_adder full_adder_2 (
    .A(A[1]), .B(B[1]), .Cin(full_adder_1_carry_out), .Sum_out(sum_out[1]), .carry_out(carry_out));
endmodule

module four_bit_adder (
  input  cin,
  input  [3:0] A,
  input  [3:0] B,
  output [3:0] sum_out,
  output cout
);

  wire two_bit_adder_1_carry_out;

  two_bit_adder two_bit_adder_1 (
    .cin(cin), .A(A[1:0]), .B(B[1:0]), .sum_out(sum_out[1:0]), .carry_out(two_bit_adder_1_carry_out));
  two_bit_adder two_bit_adder_2 (
    .cin(two_bit_adder_1_carry_out), .A(A[3:2]), .B(B[3:2]), .sum_out(sum_out[3:2]), .carry_out(cout));
endmodule

module eight_bit_adder (
  input  cin,
  input  [7:0] A,
  input  [7:0] B,
  output [7:0] sum_out,
  output cout
);

  wire four_bit_adder_1_cout;

  four_bit_adder four_bit_adder_1 (
    .cin(cin), .A(A[3:0]), .B(B[3:0]), .sum_out(sum_out[3:0]), .cout(four_bit_adder_1_cout));
  four_bit_adder four_bit_adder_2 (
    .cin(four_bit_adder_1_cout), .A(A[7:4]), .B(B[7:4]), .sum_out(sum_out[7:4]), .cout(cout));
endmodule

module sixteen_bit_adder (
  input  cin,
  input  [15:0] A,
  input  [15:0] B,
  output [15:0] sum_out,
  output cout
);

  wire eight_bit_adder_1_cout;

  eight_bit_adder eight_bit_adder_1 (
    .cin(cin), .A(A[7:0]), .B(B[7:0]), .sum_out(sum_out[7:0]), .cout(eight_bit_adder_1_cout));
  eight_bit_adder eight_bit_adder_2 (
    .cin(eight_bit_adder_1_cout), .A(A[15:8]), .B(B[15:8]), .sum_out(sum_out[15:8]), .cout(cout));
endmodule

module thirtyTwo_bit_Adder (
  input  cin,
  input  [31:0] A,
  input  [31:0] B,
  output [31:0] sum_out,
  output cout
);

  wire sixteen_bit_adder_1_cout;

  sixteen_bit_adder sixteen_bit_adder_1 (
    .cin(cin), .A(A[15:0]), .B(B[15:0]), .sum_out(sum_out[15:0]), .cout(sixteen_bit_adder_1_cout));
  sixteen_bit_adder sixteen_bit_adder_2 (
    .cin(sixteen_bit_adder_1_cout), .A(A[31:16]), .B(B[31:16]), .sum_out(sum_out[31:16]), .cout(cout));
endmodule

module sixtyFour_bit_Adder (
  input  cin,
  input  [63:0] A,
  input  [63:0] B,
  output [63:0] sum_out,
  output cout
);

  wire thirtytwo_bit_adder_1_cout;

  thirtyTwo_bit_Adder thirtytwo_bit_adder_1 (
    .cin(cin), .A(A[31:0]), .B(B[31:0]), .sum_out(sum_out[31:0]), .cout(thirtytwo_bit_adder_1_cout));
  thirtyTwo_bit_Adder thirtytwo_bit_adder_2 (
    .cin(thirtytwo_bit_adder_1_cout), .A(A[63:32]), .B(B[63:32]), .sum_out(sum_out[63:32]), .cout(cout));
endmodule

module matrixAdder2x2Core (
  input  [63:0] A11,
  input  [63:0] A12,
  input  [63:0] A21,
  input  [63:0] A22,
  input  [63:0] B11,
  input  [63:0] B12,
  input  [63:0] B21,
  input  [63:0] B22,
  output [63:0] R11,
  output [63:0] R12,
  output [63:0] R21,
  output [63:0] R22
);

  sixtyFour_bit_Adder Node_1 (.A(A11), .B(B11), .sum_out(R11));  // open: cin, cout
  sixtyFour_bit_Adder Node_3 (.A(A21), .B(B21), .sum_out(R21));  // open: cin, cout
  sixtyFour_bit_Adder Node_2 (.A(A12), .B(B12), .sum_out(R12));  // open: cin, cout
  sixtyFour_bit_Adder Node_4 (.A(A22), .B(B22), .sum_out(R22));  // open: cin, cout
endmodule

module testBench (
  input  [63:0] in_1,
  input  [63:0] in_2,
  input  [63:0] in_3,
  input  [63:0] in_4,
  input  [63:0] in_5,
  input  [63:0] in_6,
  input  [63:0] in_7,
  input  [63:0] in_8,
  output [63:0] out_9,
  output [63:0] out_10,
  output [63:0] out_11,
  output [63:0] out_12
);

  matrixAdder2x2Core matrixadder2x2core_1 (
    .A11(in_1), .A12(in_2), .A21(in_3), .A22(in_4), .B11(in_5), .B12(in_7), .B21(in_8), .B22(in_6),
    .R11(out_9), .R12(out_10), .R21(out_11), .R22(out_12));
endmodule

module Assembly (
  input  OUTPUT_ENABLE,
  input  write_ENNBLE,
  input  WRITE_ENABLE
);

  wire clock_1_out, Delay_Counter_carry;
  wire [3:0] counter_1_q;
  wire [63:0] mat_mult_node_1_r11, mat_mult_node_1_r12, mat_mult_node_1_r21, mat_mult_node_1_r22, R_11_dout,
       RAM_A11_dout, RAM_A12_dout, RAM_A21_dout, RAM_A22_dout, RAM_B11_dout, RAM_B12_dout, RAM_B21_dout,
       RAM_B22_dout, undriven;

  Clock clock_1 (.out(clock_1_out));
  RAM #(.addrWidth(4), .dataWidth(64), .\type ("nonvolatile")) RAM_A11 (
    .addr(counter_1_q), .we(write_ENNBLE), .oe(1'b1), .clk(clock_1_out), .dout(RAM_A11_dout));  // open: din
  // Probe on RAM_A21_dout
  // Probe on RAM_B21_dout
  Counter #(.max('h2), .width(4)) Delay_Counter (
    .count(clock_1_out), .clk(clock_1_out), .carry(Delay_Counter_carry));  // open: clr, load, up, D, Q
  // Probe on RAM_A11_dout
  RAM #(.addrWidth(4), .dataWidth(64), .\type ("nonvolatile")) RAM_A12 (
    .addr(counter_1_q), .we(write_ENNBLE), .clk(clock_1_out), .dout(RAM_A12_dout));  // open: oe, din
  Counter #(.max('h7), .width(4)) counter_1 (
    .count(Delay_Counter_carry), .clk(clock_1_out), .Q(counter_1_q));  // open: clr, load, up, D, carry
  mat_mult_node mat_mult_node_1 (
    .A11(RAM_A11_dout), .A12(RAM_A12_dout), .A21(RAM_A21_dout), .A22(RAM_A22_dout), .B11(RAM_B11_dout),
    .B12(RAM_B12_dout), .B21(RAM_B21_dout), .B22(RAM_B22_dout), .R11(mat_mult_node_1_r11),
    .R12(mat_mult_node_1_r12), .R21(mat_mult_node_1_r21), .R22(mat_mult_node_1_r22));
  RAM #(.addrWidth(4), .dataWidth(64), .\type ("nonvolatile")) RAM_A21 (
    .addr(counter_1_q), .we(write_ENNBLE), .oe(1'b1), .clk(clock_1_out), .dout(RAM_A21_dout));  // open: din
  // Probe on mat_mult_node_1_r11
  // Probe on mat_mult_node_1_r12
  RAM #(.addrWidth(4), .dataWidth(64), .\type ("nonvolatile")) RAM_A22 (
    .addr(counter_1_q), .we(write_ENNBLE), .oe(1'b1), .clk(clock_1_out), .dout(RAM_A22_dout));  // open: din
  RAM #(.addrWidth(4), .dataWidth(64)) R_11 (
    .addr(counter_1_q), .we(1'b1), .clk(clock_1_out), .din(mat_mult_node_1_r11), .dout(R_11_dout));  // open: oe
  // Probe on mat_mult_node_1_r21
  RAM #(.addrWidth(4), .dataWidth(64), .\type ("nonvolatile")) RAM_B11 (
    .addr(counter_1_q), .we(write_ENNBLE), .oe(1'b1), .clk(clock_1_out), .din(undriven), .dout(RAM_B11_dout));
  // Probe on mat_mult_node_1_r22
  RAM #(.addrWidth(4), .dataWidth(64), .\type ("nonvolatile")) RAM_B12 (
    .addr(counter_1_q), .we(write_ENNBLE), .oe(1'b1), .clk(clock_1_out), .dout(RAM_B12_dout));  // open: din
  RAM #(.addrWidth(4), .dataWidth(64)) R_12 (
    .addr(counter_1_q), .we(1'b1), .clk(clock_1_out), .din(mat_mult_node_1_r12));  // open: oe, dout
  RAM #(.addrWidth(4), .dataWidth(64), .\type ("nonvolatile")) RAM_B21 (
    .addr(counter_1_q), .we(write_ENNBLE), .oe(1'b1), .clk(clock_1_out), .dout(RAM_B21_dout));  // open: din
  // Probe on mat_mult_node_1_r22
  RAM #(.addrWidth(4), .dataWidth(64)) R_21 (
    .addr(counter_1_q), .we(1'b1), .clk(clock_1_out), .din(mat_mult_node_1_r22));  // open: oe, dout
  RAM #(.addrWidth(4), .dataWidth(64), .\type ("nonvolatile")) RAM_B22 (
    .addr(counter_1_q), .we(write_ENNBLE), .oe(1'b1), .clk(clock_1_out), .dout(RAM_B22_dout));  // open: din
  RAM #(.addrWidth(4), .dataWidth(64)) R_22 (
    .addr(counter_1_q), .we(1'b1), .clk(clock_1_out), .din(mat_mult_node_1_r21));  // open: oe, dout

  // Notes on the sheet:
  //   Matrix_A
  //   Matrix_B
endmodule

module counterdemo (
  input  in_1,
  input  in_2,
  input  in_3,
  input  in_4,
  input  [3:0] in_5,
  output [3:0] out_6
);

  Counter #(.max('h3), .ongoal("load"), .width(4)) counter_1 (
    .load(in_1), .up(in_2), .count(in_3), .clk(in_4), .D(in_5), .Q(out_6));  // open: clr, carry
endmodule

module Assembly48Rams (
  input  WRITE_ENABLE,
  input  OUTPUT_ENABLE,
  input  in_3,
  input  in_4,
  input  in_5
);

  wire clock_1_out;
  wire [63:0] matrixadder2x2core_1_r11, matrixadder2x2core_1_r12, matrixadder2x2core_1_r21,
       matrixadder2x2core_1_r22, matrixadder2x2core_2_r11, matrixadder2x2core_2_r12,
       matrixadder2x2core_2_r21, matrixadder2x2core_2_r22, matrixadder2x2core_3_r11,
       matrixadder2x2core_3_r12, matrixadder2x2core_3_r21, matrixadder2x2core_3_r22,
       matrixadder2x2core_4_r11, matrixadder2x2core_4_r12, matrixadder2x2core_4_r21,
       matrixadder2x2core_4_r22, ram_1_dout, ram_2_dout, ram_3_dout, ram_4_dout, ram_5_dout, ram_6_dout,
       ram_7_dout, ram_8_dout, ram_9_dout, ram_10_dout, ram_11_dout, ram_12_dout, ram_13_dout, ram_14_dout,
       ram_15_dout, ram_16_dout, ram_17_dout, ram_18_dout, ram_19_dout, ram_20_dout, ram_21_dout,
       ram_22_dout, ram_23_dout, ram_24_dout, ram_25_dout, ram_26_dout, ram_27_dout, ram_28_dout,
       ram_29_dout, ram_30_dout, ram_31_dout, ram_32_dout;

  RAM #(.addrWidth(4), .dataWidth(64), .\type ("nonvolatile")) ram_1 (
    .oe(in_5), .clk(clock_1_out), .dout(ram_1_dout));  // open: addr, we, din
  RAM #(.addrWidth(4), .dataWidth(64), .\type ("nonvolatile")) ram_2 (
    .oe(OUTPUT_ENABLE), .clk(clock_1_out), .dout(ram_2_dout));  // open: addr, we, din
  RAM #(.addrWidth(4), .dataWidth(64)) ram_3 (.oe(in_3), .clk(clock_1_out), .dout(ram_3_dout));  // open: addr, we, din
  RAM #(.addrWidth(4), .dataWidth(64), .\type ("nonvolatile")) ram_4 (
    .oe(in_4), .clk(clock_1_out), .dout(ram_4_dout));  // open: addr, we, din
  RAM #(.addrWidth(4), .dataWidth(64)) ram_5 (.oe(in_5), .clk(clock_1_out), .dout(ram_5_dout));  // open: addr, we, din
  RAM #(.addrWidth(4), .dataWidth(64)) ram_6 (
    .oe(OUTPUT_ENABLE), .clk(clock_1_out), .dout(ram_6_dout));  // open: addr, we, din
  RAM #(.addrWidth(4), .dataWidth(64)) ram_7 (.oe(in_3), .clk(clock_1_out), .dout(ram_7_dout));  // open: addr, we, din
  RAM #(.addrWidth(4), .dataWidth(64)) ram_8 (.oe(in_4), .clk(clock_1_out), .dout(ram_8_dout));  // open: addr, we, din
  RAM #(.addrWidth(4), .dataWidth(64)) ram_9 (.oe(in_5), .clk(clock_1_out), .dout(ram_9_dout));  // open: addr, we, din
  RAM #(.addrWidth(4), .dataWidth(64)) ram_10 (
    .oe(OUTPUT_ENABLE), .clk(clock_1_out), .dout(ram_10_dout));  // open: addr, we, din
  RAM #(.addrWidth(4), .dataWidth(64)) ram_11 (
    .oe(in_3), .clk(clock_1_out), .dout(ram_11_dout));  // open: addr, we, din
  RAM #(.addrWidth(4), .dataWidth(64)) ram_12 (
    .oe(in_4), .clk(clock_1_out), .dout(ram_12_dout));  // open: addr, we, din
  RAM #(.addrWidth(4), .dataWidth(64)) ram_13 (
    .oe(in_5), .clk(clock_1_out), .dout(ram_13_dout));  // open: addr, we, din
  RAM #(.addrWidth(4), .dataWidth(64)) ram_14 (
    .oe(OUTPUT_ENABLE), .clk(clock_1_out), .dout(ram_14_dout));  // open: addr, we, din
  RAM #(.addrWidth(4), .dataWidth(64)) ram_15 (
    .oe(in_3), .clk(clock_1_out), .dout(ram_15_dout));  // open: addr, we, din
  RAM #(.addrWidth(4), .dataWidth(64)) ram_16 (
    .oe(in_4), .clk(clock_1_out), .dout(ram_16_dout));  // open: addr, we, din
  RAM #(.addrWidth(4), .dataWidth(64)) ram_17 (
    .oe(in_5), .clk(clock_1_out), .dout(ram_17_dout));  // open: addr, we, din
  RAM #(.addrWidth(4), .dataWidth(64)) ram_18 (
    .oe(OUTPUT_ENABLE), .clk(clock_1_out), .dout(ram_18_dout));  // open: addr, we, din
  RAM #(.addrWidth(4), .dataWidth(64)) ram_19 (
    .oe(in_3), .clk(clock_1_out), .dout(ram_19_dout));  // open: addr, we, din
  RAM #(.addrWidth(4), .dataWidth(64)) ram_20 (
    .oe(in_4), .clk(clock_1_out), .dout(ram_20_dout));  // open: addr, we, din
  RAM #(.addrWidth(4), .dataWidth(64)) ram_21 (
    .oe(in_5), .clk(clock_1_out), .dout(ram_21_dout));  // open: addr, we, din
  RAM #(.addrWidth(4), .dataWidth(64)) ram_22 (
    .oe(OUTPUT_ENABLE), .clk(clock_1_out), .dout(ram_22_dout));  // open: addr, we, din
  RAM #(.addrWidth(4), .dataWidth(64)) ram_23 (
    .oe(in_3), .clk(clock_1_out), .dout(ram_23_dout));  // open: addr, we, din
  RAM #(.addrWidth(4), .dataWidth(64)) ram_24 (
    .oe(in_4), .clk(clock_1_out), .dout(ram_24_dout));  // open: addr, we, din
  RAM #(.addrWidth(4), .dataWidth(64)) ram_25 (
    .oe(in_5), .clk(clock_1_out), .dout(ram_25_dout));  // open: addr, we, din
  RAM #(.addrWidth(4), .dataWidth(64)) ram_26 (
    .oe(OUTPUT_ENABLE), .clk(clock_1_out), .dout(ram_26_dout));  // open: addr, we, din
  RAM #(.addrWidth(4), .dataWidth(64)) ram_27 (
    .oe(in_3), .clk(clock_1_out), .dout(ram_27_dout));  // open: addr, we, din
  RAM #(.addrWidth(4), .dataWidth(64)) ram_28 (
    .oe(in_4), .clk(clock_1_out), .dout(ram_28_dout));  // open: addr, we, din
  RAM #(.addrWidth(4), .dataWidth(64)) ram_29 (
    .oe(in_5), .clk(clock_1_out), .dout(ram_29_dout));  // open: addr, we, din
  RAM #(.addrWidth(4), .dataWidth(64)) ram_30 (
    .oe(OUTPUT_ENABLE), .clk(clock_1_out), .dout(ram_30_dout));  // open: addr, we, din
  RAM #(.addrWidth(4), .dataWidth(64)) ram_31 (
    .oe(in_3), .clk(clock_1_out), .dout(ram_31_dout));  // open: addr, we, din
  RAM #(.addrWidth(4), .dataWidth(64)) ram_32 (
    .oe(in_4), .clk(clock_1_out), .dout(ram_32_dout));  // open: addr, we, din
  matrixAdder2x2Core matrixadder2x2core_1 (
    .A11(ram_1_dout), .A12(ram_5_dout), .A21(ram_9_dout), .A22(ram_13_dout), .B11(ram_17_dout),
    .B12(ram_21_dout), .B21(ram_25_dout), .B22(ram_29_dout), .R11(matrixadder2x2core_1_r11),
    .R12(matrixadder2x2core_1_r12), .R21(matrixadder2x2core_1_r21), .R22(matrixadder2x2core_1_r22));
  matrixAdder2x2Core matrixadder2x2core_2 (
    .A11(ram_2_dout), .A12(ram_6_dout), .A21(ram_10_dout), .A22(ram_14_dout), .B11(ram_18_dout),
    .B12(ram_22_dout), .B21(ram_26_dout), .B22(ram_30_dout), .R11(matrixadder2x2core_2_r11),
    .R12(matrixadder2x2core_2_r12), .R21(matrixadder2x2core_2_r21), .R22(matrixadder2x2core_2_r22));
  matrixAdder2x2Core matrixadder2x2core_3 (
    .A11(ram_3_dout), .A12(ram_7_dout), .A21(ram_11_dout), .A22(ram_15_dout), .B11(ram_19_dout),
    .B12(ram_23_dout), .B21(ram_27_dout), .B22(ram_31_dout), .R11(matrixadder2x2core_3_r11),
    .R12(matrixadder2x2core_3_r12), .R21(matrixadder2x2core_3_r21), .R22(matrixadder2x2core_3_r22));
  matrixAdder2x2Core matrixadder2x2core_4 (
    .A11(ram_4_dout), .A12(ram_8_dout), .A21(ram_12_dout), .A22(ram_16_dout), .B11(ram_20_dout),
    .B12(ram_24_dout), .B21(ram_28_dout), .B22(ram_32_dout), .R11(matrixadder2x2core_4_r11),
    .R12(matrixadder2x2core_4_r12), .R21(matrixadder2x2core_4_r21), .R22(matrixadder2x2core_4_r22));
  RAM #(.addrWidth(4), .dataWidth(64)) ram_33 (
    .we(WRITE_ENABLE), .clk(clock_1_out), .din(matrixadder2x2core_1_r11));  // open: addr, oe, dout
  RAM #(.addrWidth(4), .dataWidth(64)) ram_34 (
    .we(WRITE_ENABLE), .clk(clock_1_out), .din(matrixadder2x2core_2_r11));  // open: addr, oe, dout
  RAM #(.addrWidth(4), .dataWidth(64)) ram_35 (
    .we(WRITE_ENABLE), .clk(clock_1_out), .din(matrixadder2x2core_3_r11));  // open: addr, oe, dout
  RAM #(.addrWidth(4), .dataWidth(64)) ram_36 (
    .we(WRITE_ENABLE), .clk(clock_1_out), .din(matrixadder2x2core_4_r11));  // open: addr, oe, dout
  RAM #(.addrWidth(4), .dataWidth(64)) ram_37 (
    .we(WRITE_ENABLE), .clk(clock_1_out), .din(matrixadder2x2core_1_r12));  // open: addr, oe, dout
  RAM #(.addrWidth(4), .dataWidth(64)) ram_38 (
    .we(WRITE_ENABLE), .clk(clock_1_out), .din(matrixadder2x2core_2_r12));  // open: addr, oe, dout
  RAM #(.addrWidth(4), .dataWidth(64)) ram_39 (
    .we(WRITE_ENABLE), .clk(clock_1_out), .din(matrixadder2x2core_3_r12));  // open: addr, oe, dout
  RAM #(.addrWidth(4), .dataWidth(64)) ram_40 (
    .we(WRITE_ENABLE), .clk(clock_1_out), .din(matrixadder2x2core_4_r12));  // open: addr, oe, dout
  RAM #(.addrWidth(4), .dataWidth(64)) ram_41 (
    .we(WRITE_ENABLE), .clk(clock_1_out), .din(matrixadder2x2core_1_r22));  // open: addr, oe, dout
  RAM #(.addrWidth(4), .dataWidth(64)) ram_42 (
    .we(WRITE_ENABLE), .clk(clock_1_out), .din(matrixadder2x2core_2_r22));  // open: addr, oe, dout
  RAM #(.addrWidth(4), .dataWidth(64)) ram_43 (
    .we(WRITE_ENABLE), .clk(clock_1_out), .din(matrixadder2x2core_3_r22));  // open: addr, oe, dout
  RAM #(.addrWidth(4), .dataWidth(64)) ram_44 (
    .we(WRITE_ENABLE), .clk(clock_1_out), .din(matrixadder2x2core_4_r22));  // open: addr, oe, dout
  RAM #(.addrWidth(4), .dataWidth(64)) ram_45 (
    .we(WRITE_ENABLE), .clk(clock_1_out), .din(matrixadder2x2core_1_r21));  // open: addr, oe, dout
  RAM #(.addrWidth(4), .dataWidth(64)) ram_46 (
    .we(WRITE_ENABLE), .clk(clock_1_out), .din(matrixadder2x2core_2_r21));  // open: addr, oe, dout
  RAM #(.addrWidth(4), .dataWidth(64)) ram_47 (
    .we(WRITE_ENABLE), .clk(clock_1_out), .din(matrixadder2x2core_3_r21));  // open: addr, oe, dout
  RAM #(.addrWidth(4), .dataWidth(64)) ram_48 (
    .we(WRITE_ENABLE), .clk(clock_1_out), .din(matrixadder2x2core_4_r21));  // open: addr, oe, dout
  Clock clock_1 (.out(clock_1_out));
endmodule

module assembly2 (
  input  OUTPUT_ENABLE,
  input  WE,
  input  OE,
  input  WRITE_ENABLE
);

  wire clock_1_out, Delay_Counter_carry;
  wire [4:0] counter_1_q;
  wire [63:0] matrixadder2x2core_1_r11, matrixadder2x2core_1_r12, matrixadder2x2core_1_r21,
       matrixadder2x2core_1_r22, R_11_dout, R_12_dout, R_21_dout, R_22_dout, RAM_A11_dout, RAM_A12_dout,
       RAM_A21_dout, RAM_A22_dout, RAM_B11_dout, RAM_B12_dout, RAM_B21_dout, RAM_B22_dout;

  Clock clock_1 (.out(clock_1_out));
  RAM #(.addrWidth(5), .dataWidth(64), .\type ("nonvolatile")) RAM_A11 (
    .addr(counter_1_q), .we(WE), .oe(1'b1), .clk(clock_1_out), .din(R_11_dout), .dout(RAM_A11_dout));
  // Probe on RAM_B12_dout
  Counter #(.max('h2), .width(4)) Delay_Counter (
    .count(clock_1_out), .clk(clock_1_out), .carry(Delay_Counter_carry));  // open: clr, load, up, D, Q
  // Probe on RAM_A12_dout
  // Probe on RAM_A11_dout
  RAM #(.addrWidth(5), .dataWidth(64), .\type ("nonvolatile")) RAM_A12 (
    .addr(counter_1_q), .oe(1'b1), .clk(clock_1_out), .din(R_21_dout), .dout(RAM_A12_dout));  // open: we
  Counter #(.max('h7), .width(5)) counter_1 (
    .count(Delay_Counter_carry), .clk(clock_1_out), .Q(counter_1_q));  // open: clr, load, up, D, carry
  matrixAdder2x2Core matrixadder2x2core_1 (
    .A11(RAM_A11_dout), .A12(RAM_A12_dout), .A21(RAM_A21_dout), .A22(RAM_A22_dout), .B11(RAM_B11_dout),
    .B12(RAM_B12_dout), .B21(RAM_B21_dout), .B22(RAM_B22_dout), .R11(matrixadder2x2core_1_r11),
    .R12(matrixadder2x2core_1_r12), .R21(matrixadder2x2core_1_r21), .R22(matrixadder2x2core_1_r22));
  RAM #(.addrWidth(5), .dataWidth(64), .\type ("nonvolatile")) RAM_A21 (
    .addr(counter_1_q), .we(WE), .oe(1'b1), .clk(clock_1_out), .dout(RAM_A21_dout));  // open: din
  // Probe on matrixadder2x2core_1_r11
  // Probe on matrixadder2x2core_1_r12
  RAM #(.addrWidth(5), .dataWidth(64), .\type ("nonvolatile")) RAM_A22 (
    .addr(counter_1_q), .we(WE), .oe(1'b1), .clk(clock_1_out), .dout(RAM_A22_dout));  // open: din
  RAM #(.addrWidth(5), .dataWidth(64)) R_11 (
    .addr(counter_1_q), .we(1'b1), .oe(OE), .clk(clock_1_out), .din(matrixadder2x2core_1_r11),
    .dout(R_11_dout));
  // Probe on matrixadder2x2core_1_r21
  RAM #(.addrWidth(5), .dataWidth(64), .\type ("nonvolatile")) RAM_B11 (
    .addr(counter_1_q), .we(WE), .oe(1'b1), .clk(clock_1_out), .din(R_12_dout), .dout(RAM_B11_dout));
  // Probe on matrixadder2x2core_1_r12
  RAM #(.addrWidth(5), .dataWidth(64), .\type ("nonvolatile")) RAM_B12 (
    .addr(counter_1_q), .we(WE), .oe(1'b1), .clk(clock_1_out), .din(R_22_dout), .dout(RAM_B12_dout));
  RAM #(.addrWidth(5), .dataWidth(64)) R_12 (
    .addr(counter_1_q), .we(1'b1), .oe(OE), .clk(clock_1_out), .din(matrixadder2x2core_1_r12),
    .dout(R_12_dout));
  RAM #(.addrWidth(5), .dataWidth(64), .\type ("nonvolatile")) RAM_B21 (
    .addr(counter_1_q), .we(WE), .oe(1'b1), .clk(clock_1_out), .dout(RAM_B21_dout));  // open: din
  RAM #(.addrWidth(5), .dataWidth(64)) R_21 (
    .addr(counter_1_q), .we(1'b1), .oe(OE), .clk(clock_1_out), .din(matrixadder2x2core_1_r22),
    .dout(R_21_dout));
  RAM #(.addrWidth(5), .dataWidth(64), .\type ("nonvolatile")) RAM_B22 (
    .addr(counter_1_q), .we(WE), .oe(1'b1), .clk(clock_1_out), .dout(RAM_B22_dout));  // open: din
  RAM #(.addrWidth(5), .dataWidth(64)) R_22 (
    .addr(counter_1_q), .we(1'b1), .oe(OE), .clk(clock_1_out), .din(matrixadder2x2core_1_r21),
    .dout(R_22_dout));

  // Notes on the sheet:
  //   Matrix_A
  //   Matrix_B
endmodule

module test_assembly (
  input  OUTPUT_ENABLE,
  input  WE,
  input  OE,
  input  WRITE_ENABLE
);

  wire clock_1_out, Delay_Counter_carry;
  wire [4:0] counter_1_q, counter_2_q;
  wire [63:0] matrixadder2x2core_1_r11, matrixadder2x2core_1_r12, matrixadder2x2core_1_r21,
       matrixadder2x2core_1_r22, R_11_dout, R_12_dout, R_21_dout, R_22_dout, RAM_A11_dout, RAM_A12_dout,
       RAM_A21_dout, RAM_A22_dout, RAM_B11_dout, RAM_B12_dout, RAM_B21_dout, RAM_B22_dout;

  Clock clock_1 (.out(clock_1_out));
  RAM #(.addrWidth(5), .dataWidth(64), .\type ("nonvolatile")) RAM_A11 (
    .addr(counter_2_q), .we(WE), .oe(1'b1), .clk(clock_1_out), .din(R_11_dout), .dout(RAM_A11_dout));
  // Probe on RAM_B12_dout
  Counter #(.max('h2), .width(4)) Delay_Counter (
    .count(clock_1_out), .clk(clock_1_out), .carry(Delay_Counter_carry));  // open: clr, load, up, D, Q
  // Probe on RAM_A12_dout
  // Probe on RAM_A11_dout
  Counter #(.max('h7), .width(5)) counter_1 (
    .clk(clock_1_out), .Q(counter_1_q));  // open: clr, load, up, count, D, carry
  RAM #(.addrWidth(5), .dataWidth(64), .\type ("nonvolatile")) RAM_A12 (
    .addr(counter_2_q), .oe(1'b1), .clk(clock_1_out), .din(R_21_dout), .dout(RAM_A12_dout));  // open: we
  Counter #(.max('h18), .width(5)) counter_2 (
    .count(Delay_Counter_carry), .clk(clock_1_out), .Q(counter_2_q));  // open: clr, load, up, D, carry
  matrixAdder2x2Core matrixadder2x2core_1 (
    .A11(RAM_A11_dout), .A12(RAM_A12_dout), .A21(RAM_A21_dout), .A22(RAM_A22_dout), .B11(RAM_B11_dout),
    .B12(RAM_B12_dout), .B21(RAM_B21_dout), .B22(RAM_B22_dout), .R11(matrixadder2x2core_1_r11),
    .R12(matrixadder2x2core_1_r12), .R21(matrixadder2x2core_1_r21), .R22(matrixadder2x2core_1_r22));
  RAM #(.addrWidth(5), .dataWidth(64), .\type ("nonvolatile")) RAM_A21 (
    .addr(counter_2_q), .we(WE), .oe(1'b1), .clk(clock_1_out), .dout(RAM_A21_dout));  // open: din
  // Probe on matrixadder2x2core_1_r11
  // Probe on matrixadder2x2core_1_r12
  RAM #(.addrWidth(5), .dataWidth(64), .\type ("nonvolatile")) RAM_A22 (
    .addr(counter_2_q), .we(WE), .oe(1'b1), .clk(clock_1_out), .dout(RAM_A22_dout));  // open: din
  RAM #(.addrWidth(5), .dataWidth(64)) R_11 (
    .addr(counter_1_q), .we(1'b1), .oe(OE), .clk(clock_1_out), .din(matrixadder2x2core_1_r11),
    .dout(R_11_dout));
  // Probe on matrixadder2x2core_1_r21
  RAM #(.addrWidth(5), .dataWidth(64), .\type ("nonvolatile")) RAM_B11 (
    .addr(counter_2_q), .we(WE), .oe(1'b1), .clk(clock_1_out), .din(R_12_dout), .dout(RAM_B11_dout));
  // Probe on matrixadder2x2core_1_r12
  RAM #(.addrWidth(5), .dataWidth(64), .\type ("nonvolatile")) RAM_B12 (
    .addr(counter_2_q), .we(WE), .oe(1'b1), .clk(clock_1_out), .din(R_22_dout), .dout(RAM_B12_dout));
  RAM #(.addrWidth(5), .dataWidth(64)) R_12 (
    .addr(counter_1_q), .we(1'b1), .oe(OE), .clk(clock_1_out), .din(matrixadder2x2core_1_r12),
    .dout(R_12_dout));
  RAM #(.addrWidth(5), .dataWidth(64), .\type ("nonvolatile")) RAM_B21 (
    .addr(counter_2_q), .we(WE), .oe(1'b1), .clk(clock_1_out), .dout(RAM_B21_dout));  // open: din
  RAM #(.addrWidth(5), .dataWidth(64)) R_21 (
    .addr(counter_1_q), .we(1'b1), .oe(OE), .clk(clock_1_out), .din(matrixadder2x2core_1_r22),
    .dout(R_21_dout));
  RAM #(.addrWidth(5), .dataWidth(64), .\type ("nonvolatile")) RAM_B22 (
    .addr(counter_2_q), .we(WE), .oe(1'b1), .clk(clock_1_out), .dout(RAM_B22_dout));  // open: din
  RAM #(.addrWidth(5), .dataWidth(64)) R_22 (
    .addr(counter_1_q), .we(1'b1), .oe(OE), .clk(clock_1_out), .din(matrixadder2x2core_1_r21),
    .dout(R_22_dout));

  // Notes on the sheet:
  //   Matrix_A
  //   Matrix_B
endmodule

module multiplier_Core (
  input  [63:0] A11,
  input  [63:0] B11,
  input  [63:0] A12,
  input  [63:0] B12,
  input  [63:0] A21,
  input  [63:0] B21,
  input  [63:0] A22,
  input  [63:0] B22,
  output [63:0] R11,
  output [63:0] xtra64bits,
  output [63:0] R12,
  output [63:0] xtra64bits2,
  output [63:0] R21,
  output [63:0] xtra64bits3,
  output [63:0] R22,
  output [63:0] xtra64bits4
);

  // Probe on A11
  // Probe on A12
  // Probe on A21
  // Probe on A22
  // Probe on B11
  // Probe on B12
  // Probe on B21
  // Probe on B22
  Multiplier #(.width(64)) multiplier_1 (.a(A11), .b(B11), .out(R11), .cout(xtra64bits));  // open: cin
  Multiplier #(.width(64)) multiplier_2 (.a(A12), .b(B12), .out(R12), .cout(xtra64bits2));  // open: cin
  Multiplier #(.width(64)) multiplier_3 (.a(A21), .b(B21), .out(R21), .cout(xtra64bits3));  // open: cin
  Multiplier #(.width(64)) multiplier_4 (.a(A22), .b(B22), .out(R22), .cout(xtra64bits4));  // open: cin
  // Probe on R11
  // Probe on R12
  // Probe on R21
  // Probe on R22
endmodule

module mat_mult_node (
  input  [63:0] A11,
  input  [63:0] A12,
  input  [63:0] A21,
  input  [63:0] A22,
  input  [63:0] B11,
  input  [63:0] B12,
  input  [63:0] B21,
  input  [63:0] B22,
  output [63:0] R11,
  output [63:0] R12,
  output [63:0] R21,
  output [63:0] R22
);

  wire [63:0] multiplier_1_out, multiplier_2_out, multiplier_3_out, multiplier_4_out, multiplier_5_out,
       multiplier_6_out, multiplier_7_out, multiplier_8_out;

  // Probe on A12
  // Probe on B11
  // Probe on B21
  // Probe on A11
  // Probe on A21
  // Probe on B11
  Multiplier #(.width(64)) multiplier_1 (.a(A11), .b(B11), .out(multiplier_1_out));  // open: cin, cout
  Multiplier #(.width(64)) multiplier_2 (.a(A12), .b(B21), .out(multiplier_2_out));  // open: cin, cout
  Multiplier #(.width(64)) multiplier_3 (.a(A11), .b(B12), .out(multiplier_3_out));  // open: cin, cout
  Multiplier #(.width(64)) multiplier_4 (.a(A12), .b(B22), .out(multiplier_4_out));  // open: cin, cout
  Multiplier #(.width(64)) multiplier_5 (.a(A21), .b(B11), .out(multiplier_5_out));  // open: cin, cout
  Multiplier #(.width(64)) multiplier_6 (.a(A22), .b(B21), .out(multiplier_6_out));  // open: cin, cout
  Multiplier #(.width(64)) multiplier_7 (.a(A21), .b(B12), .out(multiplier_7_out));  // open: cin, cout
  Multiplier #(.width(64)) multiplier_8 (.a(A22), .b(B22), .out(multiplier_8_out));  // open: cin, cout
  sixtyFour_bit_Adder sixtyfour_bit_adder_1 (
    .A(multiplier_1_out), .B(multiplier_2_out), .sum_out(R11));  // open: cin, cout
  sixtyFour_bit_Adder sixtyfour_bit_adder_2 (
    .A(multiplier_3_out), .B(multiplier_4_out), .sum_out(R12));  // open: cin, cout
  sixtyFour_bit_Adder sixtyfour_bit_adder_3 (
    .A(multiplier_5_out), .B(multiplier_6_out), .sum_out(R21));  // open: cin, cout
  sixtyFour_bit_Adder sixtyfour_bit_adder_4 (
    .A(multiplier_7_out), .B(multiplier_8_out), .sum_out(R22));  // open: cin, cout
  // Probe on R21
endmodule

module Assembly_With_MatMult (
  input  OUTPUT_ENABLE,
  input  write_ENNBLE,
  input  WRITE_ENABLE
);

  wire clock_1_out, Delay_Counter_carry;
  wire [3:0] counter_1_q;
  wire [63:0] mat_mult_node_1_r11, mat_mult_node_1_r12, mat_mult_node_1_r21, mat_mult_node_1_r22, R_11_dout,
       RAM_A11_dout, RAM_A12_dout, RAM_A21_dout, RAM_A22_dout, RAM_B11_dout, RAM_B12_dout, RAM_B21_dout,
       RAM_B22_dout, undriven;

  Clock clock_1 (.out(clock_1_out));
  RAM #(.addrWidth(4), .dataWidth(64), .\type ("nonvolatile")) RAM_A11 (
    .addr(counter_1_q), .we(write_ENNBLE), .oe(1'b1), .clk(clock_1_out), .dout(RAM_A11_dout));  // open: din
  // Probe on RAM_A21_dout
  // Probe on RAM_B21_dout
  Counter #(.max('h2), .width(4)) Delay_Counter (
    .count(clock_1_out), .clk(clock_1_out), .carry(Delay_Counter_carry));  // open: clr, load, up, D, Q
  // Probe on RAM_A11_dout
  RAM #(.addrWidth(4), .dataWidth(64), .\type ("nonvolatile")) RAM_A12 (
    .addr(counter_1_q), .we(write_ENNBLE), .clk(clock_1_out), .dout(RAM_A12_dout));  // open: oe, din
  Counter #(.max('h7), .width(4)) counter_1 (
    .count(Delay_Counter_carry), .clk(clock_1_out), .Q(counter_1_q));  // open: clr, load, up, D, carry
  mat_mult_node mat_mult_node_1 (
    .A11(RAM_A11_dout), .A12(RAM_A12_dout), .A21(RAM_A21_dout), .A22(RAM_A22_dout), .B11(RAM_B11_dout),
    .B12(RAM_B12_dout), .B21(RAM_B21_dout), .B22(RAM_B22_dout), .R11(mat_mult_node_1_r11),
    .R12(mat_mult_node_1_r12), .R21(mat_mult_node_1_r21), .R22(mat_mult_node_1_r22));
  RAM #(.addrWidth(4), .dataWidth(64), .\type ("nonvolatile")) RAM_A21 (
    .addr(counter_1_q), .we(write_ENNBLE), .oe(1'b1), .clk(clock_1_out), .dout(RAM_A21_dout));  // open: din
  // Probe on mat_mult_node_1_r11
  // Probe on mat_mult_node_1_r12
  RAM #(.addrWidth(4), .dataWidth(64), .\type ("nonvolatile")) RAM_A22 (
    .addr(counter_1_q), .we(write_ENNBLE), .oe(1'b1), .clk(clock_1_out), .dout(RAM_A22_dout));  // open: din
  RAM #(.addrWidth(4), .dataWidth(64)) R_11 (
    .addr(counter_1_q), .we(1'b1), .clk(clock_1_out), .din(mat_mult_node_1_r11), .dout(R_11_dout));  // open: oe
  // Probe on mat_mult_node_1_r21
  RAM #(.addrWidth(4), .dataWidth(64), .\type ("nonvolatile")) RAM_B11 (
    .addr(counter_1_q), .we(write_ENNBLE), .oe(1'b1), .clk(clock_1_out), .din(undriven), .dout(RAM_B11_dout));
  // Probe on mat_mult_node_1_r22
  RAM #(.addrWidth(4), .dataWidth(64), .\type ("nonvolatile")) RAM_B12 (
    .addr(counter_1_q), .we(write_ENNBLE), .oe(1'b1), .clk(clock_1_out), .dout(RAM_B12_dout));  // open: din
  RAM #(.addrWidth(4), .dataWidth(64)) R_12 (
    .addr(counter_1_q), .we(1'b1), .clk(clock_1_out), .din(mat_mult_node_1_r12));  // open: oe, dout
  RAM #(.addrWidth(4), .dataWidth(64), .\type ("nonvolatile")) RAM_B21 (
    .addr(counter_1_q), .we(write_ENNBLE), .oe(1'b1), .clk(clock_1_out), .dout(RAM_B21_dout));  // open: din
  // Probe on mat_mult_node_1_r22
  RAM #(.addrWidth(4), .dataWidth(64)) R_21 (
    .addr(counter_1_q), .we(1'b1), .clk(clock_1_out), .din(mat_mult_node_1_r22));  // open: oe, dout
  RAM #(.addrWidth(4), .dataWidth(64), .\type ("nonvolatile")) RAM_B22 (
    .addr(counter_1_q), .we(write_ENNBLE), .oe(1'b1), .clk(clock_1_out), .dout(RAM_B22_dout));  // open: din
  RAM #(.addrWidth(4), .dataWidth(64)) R_22 (
    .addr(counter_1_q), .we(1'b1), .clk(clock_1_out), .din(mat_mult_node_1_r21));  // open: oe, dout

  // Notes on the sheet:
  //   Matrix_A
  //   Matrix_B
endmodule

module debugger_or_sumshi (
  input  [1:0] in_1,
  output ioe,
  output owe,
  output ooe,
  output iwe
);

  wire not_1_out;

  not not_1 (not_1_out, in_1[1]);
  and and_1 (ioe, ~in_1[0], ~in_1[1]);  // AND_Gate
  and and_2 (owe, in_1[0], not_1_out);
  and and_3 (ooe, ~in_1[0], in_1[1]);  // AND_Gate
  and and_4 (iwe, in_1[0], in_1[1]);
endmodule

module mat_mult_4x4 (
  input  [63:0] A11_11,
  input  [63:0] A11_12,
  input  [63:0] A11_21,
  input  [63:0] A11_22,
  input  [63:0] A12_11,
  input  [63:0] A12_12,
  input  [63:0] A12_21,
  input  [63:0] A12_22,
  input  [63:0] B11_11,
  input  [63:0] B11_12,
  input  [63:0] B11_21,
  input  [63:0] B11_22,
  input  [63:0] B21_11,
  input  [63:0] B21_12,
  input  [63:0] B21_21,
  input  [63:0] B21_22,
  output [63:0] R11,
  output [63:0] R12,
  output [63:0] R22,
  output [63:0] R21
);

  wire [63:0] mat_mult_node_1_r11, mat_mult_node_1_r12, mat_mult_node_1_r21, mat_mult_node_1_r22,
       mat_mult_node_2_r11, mat_mult_node_2_r12, mat_mult_node_2_r21, mat_mult_node_2_r22;

  mat_mult_node mat_mult_node_1 (
    .A11(A12_11), .A12(A12_12), .A21(A12_21), .A22(A12_22), .B11(B21_11), .B12(B21_12), .B21(B21_21),
    .B22(B21_22), .R11(mat_mult_node_1_r11), .R12(mat_mult_node_1_r12), .R21(mat_mult_node_1_r21),
    .R22(mat_mult_node_1_r22));
  mat_mult_node mat_mult_node_2 (
    .A11(A11_11), .A12(A11_12), .A21(A11_21), .A22(A11_22), .B11(B11_11), .B12(B11_12), .B21(B11_21),
    .B22(B11_22), .R11(mat_mult_node_2_r11), .R12(mat_mult_node_2_r12), .R21(mat_mult_node_2_r21),
    .R22(mat_mult_node_2_r22));
  matrixAdder2x2Core matrixadder2x2core_1 (
    .A11(mat_mult_node_2_r11), .A12(mat_mult_node_2_r12), .A21(mat_mult_node_2_r21),
    .A22(mat_mult_node_2_r22), .B11(mat_mult_node_1_r11), .B12(mat_mult_node_1_r12),
    .B21(mat_mult_node_1_r21), .B22(mat_mult_node_1_r22), .R11(R11), .R12(R12), .R21(R22), .R22(R21));

  // Notes on the sheet:
  //   A11
  //   A12
  //   B11
  //   B21
endmodule
