// Logisim project July_18_TA_VIVA.circ as structural Verilog
module half_adder (
  input  A,
  input  B,
  output sum,
  output carry_out
);

  xor xor_1 (sum, A, B);
  and and_1 (carry_out, A, B);
endmodule

module full_adder (
  input  A,
  input  B,
  input  Cin,
  output Sum_out,
  output carry_out
);

  wire half_adder_1_carry_out, half_adder_1_sum, half_adder_2_carry_out;

  half_adder half_adder_1 (.A(A), .B(B), .sum(half_adder_1_sum), .carry_out(half_adder_1_carry_out));
  half_adder half_adder_2 (.A(half_adder_1_sum), .B(Cin), .sum(Sum_out), .carry_out(half_adder_2_carry_out));
  or or_1 (carry_out, half_adder_2_carry_out, half_adder_1_carry_out);
endmodule

module two_bit_adder (
  input  cin,
  input  [1:0] A,
  input  [1:0] B,
  output [1:0] sum_out,
  output carry_out
);

  wire full_adder_1_carry_out;

  full_adder full_adder_1 (.A(A[0]), .B(B[0]), .Cin(cin), .Sum_out(sum_out[0]), .carry_out(full_adder_1_carry_out));
  full_adder full_adder_2 (
    .A(A[1]), .B(B[1]), .Cin(full_adder_1_carry_out), .Sum_out(sum_out[1]), .carry_out(carry_out));
endmodule

module four_bit_adder (
  input  cin,
  input  [3:0] A,
  input  [3:0] B,
  output [3:0] sum_out,
  output cout
);

  wire two_bit_adder_1_carry_out;

  two_bit_adder two_bit_adder_1 (
    .cin(cin), .A(A[1:0]), .B(B[1:0]), .sum_out(sum_out[1:0]), .carry_out(two_bit_adder_1_carry_out));
  two_bit_adder two_bit_adder_2 (
    .cin(two_bit_adder_1_carry_out), .A(A[3:2]), .B(B[3:2]), .sum_out(sum_out[3:2]), .carry_out(cout));
endmodule

module eight_bit_adder (
  input  cin,
  input  [7:0] A,
  input  [7:0] B,
  output [7:0] sum_out,
  output cout
);

  wire four_bit_adder_1_cout;

  four_bit_adder four_bit_adder_1 (
    .cin(cin), .A(A[3:0]), .B(B[3:0]), .sum_out(sum_out[3:0]), .cout(four_bit_adder_1_cout));
  four_bit_adder four_bit_adder_2 (
    .cin(four_bit_adder_1_cout), .A(A[7:4]), .B(B[7:4]), .sum_out(sum_out[7:4]), .cout(cout));
endmodule

module sixteen_bit_adder (
  input  cin,
  input  [15:0] A,
  input  [15:0] B,
  output [15:0] sum_out,
  output cout
);

  wire eight_bit_adder_1_cout;

  eight_bit_adder eight_bit_adder_1 (
    .cin(cin), .A(A[7:0]), .B(B[7:0]), .sum_out(sum_out[7:0]), .cout(eight_bit_adder_1_cout));
  eight_bit_adder eight_bit_adder_2 (
    .cin(eight_bit_adder_1_cout), .A(A[15:8]), .B(B[15:8]), .sum_out(sum_out[15:8]), .cout(cout));
endmodule

module thirtyTwo_bit_Adder (
  input  cin,
  input  [31:0] A,
  input  [31:0] B,
  output [31:0] sum_out,
  output cout
);

  wire sixteen_bit_adder_1_cout;

  sixteen_bit_adder sixteen_bit_adder_1 (
    .cin(cin), .A(A[15:0]), .B(B[15:0]), .sum_out(sum_out[15:0]), .cout(sixteen_bit_adder_1_cout));
  sixteen_bit_adder sixteen_bit_adder_2 (
    .cin(sixteen_bit_adder_1_cout), .A(A[31:16]), .B(B[31:16]), .sum_out(sum_out[31:16]), .cout(cout));
endmodule

module sixtyFour_bit_Adder (
  input  cin,
  input  [63:0] A,
  input  [63:0] B,
  output [63:0] sum_out,
  output cout
);

  wire thirtytwo_bit_adder_1_cout;

  thirtyTwo_bit_Adder thirtytwo_bit_adder_1 (
    .cin(cin), .A(A[31:0]), .B(B[31:0]), .sum_out(sum_out[31:0]), .cout(thirtytwo_bit_adder_1_cout));
  thirtyTwo_bit_Adder thirtytwo_bit_adder_2 (
    .cin(thirtytwo_bit_adder_1_cout), .A(A[63:32]), .B(B[63:32]), .sum_out(sum_out[63:32]), .cout(cout));
endmodule

module matrixAdder2x2Core (
  input  [63:0] A11,
  input  [63:0] A12,
  input  [63:0] A21,
  input  [63:0] A22,
  input  [63:0] B11,
  input  [63:0] B12,
  input  [63:0] B21,
  input  [63:0] B22,
  output [63:0] R11,
  output [63:0] R12,
  output [63:0] R21,
  output [63:0] R22
);

  Adder #(.width(64)) adder_1 (.a(A21), .b(B21), .out(R21));  // open: cin, cout
  Adder #(.width(64)) adder_2 (.a(A11), .b(B11), .out(R11));  // open: cin, cout
  Adder #(.width(64)) adder_3 (.a(A12), .b(B12), .out(R12));  // open: cin, cout
  Adder #(.width(64)) adder_4 (.a(A22), .b(B22), .out(R22));  // open: cin, cout
endmodule

module testBench (
  input  [63:0] in_1,
  input  [63:0] in_2,
  input  [63:0] in_3,
  input  [63:0] in_4,
  input  [63:0] in_5,
  input  [63:0] in_6,
  input  [63:0] in_7,
  input  [63:0] in_8,
  output [63:0] out_9,
  output [63:0] out_10,
  output [63:0] out_11,
  output [63:0] out_12
);

  matrixAdder2x2Core matrixadder2x2core_1 (
    .A11(in_1), .A12(in_2), .A21(in_3), .A22(in_4), .B11(in_5), .B12(in_7), .B21(in_8), .B22(in_6),
    .R11(out_9), .R12(out_10), .R21(out_11), .R22(out_12));
endmodule

module Assembly (
  input  OUTPUT_ENABLE,
  input  write_ENNBLE,
  input  WRITE_ENABLE
);

  wire clock_1_out, Delay_Counter_carry;
  wire [3:0] counter_1_q;
  wire [63:0] mat_mult_node_1_r11, mat_mult_node_1_r12, mat_mult_node_1_r21, mat_mult_node_1_r22, R_11_dout,
       RAM_A11_dout, RAM_A12_dout, RAM_A21_dout, RAM_A22_dout, RAM_B11_dout, RAM_B12_dout, RAM_B21_dout,
       RAM_B22_dout, undriven;

  Clock clock_1 (.out(clock_1_out));
  RAM #(.addrWidth(4), .dataWidth(64), .\type ("nonvolatile")) RAM_A11 (
    .addr(counter_1_q), .we(write_ENNBLE), .oe(1'b1), .clk(clock_1_out), .dout(RAM_A11_dout));  // open: din
  // Probe on RAM_A21_dout
  // Probe on RAM_B21_dout
  Counter #(.max('h2), .width(4)) Delay_Counter (
    .count(clock_1_out), .clk(clock_1_out), .carry(Delay_Counter_carry));  // open: clr, load, up, D, Q
  // Probe on RAM_A11_dout
  RAM #(.addrWidth(4), .dataWidth(64), .\type ("nonvolatile")) RAM_A12 (
    .addr(counter_1_q), .we(write_ENNBLE), .clk(clock_1_out), .dout(RAM_A12_dout));  // open: oe, din
  Counter #(.max('h7), .width(4)) counter_1 (
    .count(Delay_Counter_carry), .clk(clock_1_out), .Q(counter_1_q));  // open: clr, load, up, D, carry
  mat_mult_node mat_mult_node_1 (
    .A11(RAM_A11_dout), .A12(RAM_A12_dout), .A21(RAM_A21_dout), .A22(RAM_A22_dout), .B11(RAM_B11_dout),
    .B12(RAM_B12_dout), .B21(RAM_B21_dout), .B22(RAM_B22_dout), .R11(mat_mult_node_1_r11),
    .R12(mat_mult_node_1_r12), .R21(mat_mult_node_1_r21), .R22(mat_mult_node_1_r22));
  RAM #(.addrWidth(4), .dataWidth(64), .\type ("nonvolatile")) RAM_A21 (
    .addr(counter_1_q), .we(write_ENNBLE), .oe(1'b1), .clk(clock_1_out), .dout(RAM_A21_dout));  // open: din
  // Probe on mat_mult_node_1_r11
  // Probe on mat_mult_node_1_r12
  RAM #(.addrWidth(4), .dataWidth(64), .\type ("nonvolatile")) RAM_A22 (
    .addr(counter_1_q), .we(write_ENNBLE), .oe(1'b1), .clk(clock_1_out), .dout(RAM_A22_dout));  // open: din
  RAM #(.addrWidth(4), .dataWidth(64)) R_11 (
    .addr(counter_1_q), .we(1'b1), .clk(clock_1_out), .din(mat_mult_node_1_r11), .dout(R_11_dout));  // open: oe
  // Probe on mat_mult_node_1_r21
  RAM #(.addrWidth(4), .dataWidth(64), .\type ("nonvolatile")) RAM_B11 (
    .addr(counter_1_q), .we(write_ENNBLE), .oe(1'b1), .clk(clock_1_out), .din(undriven), .dout(RAM_B11_dout));
  // Probe on mat_mult_node_1_r22
  RAM #(.addrWidth(4), .dataWidth(64), .\type ("nonvolatile")) RAM_B12 (
    .addr(counter_1_q), .we(write_ENNBLE), .oe(1'b1), .clk(clock_1_out), .dout(RAM_B12_dout));  // open: din
  RAM #(.addrWidth(4), .dataWidth(64)) R_12 (
    .addr(counter_1_q), .we(1'b1), .clk(clock_1_out), .din(mat_mult_node_1_r12));  // open: oe, dout
  RAM #(.addrWidth(4), .dataWidth(64), .\type ("nonvolatile")) RAM_B21 (
    .addr(counter_1_q), .we(write_ENNBLE), .oe(1'b1), .clk(clock_1_out), .dout(RAM_B21_dout));  // open: din
  // Probe on mat_mult_node_1_r22
  RAM #(.addrWidth(4), .dataWidth(64)) R_21 (
    .addr(counter_1_q), .we(1'b1), .clk(clock_1_out), .din(mat_mult_node_1_r22));  // open: oe, dout
  RAM #(.addrWidth(4), .dataWidth(64), .\type ("nonvolatile")) RAM_B22 (
    .addr(counter_1_q), .we(write_ENNBLE), .oe(1'b1), .clk(clock_1_out), .dout(RAM_B22_dout));  // open: din
  RAM #(.addrWidth(4), .dataWidth(64)) R_22 (
    .addr(counter_1_q), .we(1'b1), .clk(clock_1_out), .din(mat_mult_node_1_r21));  // open: oe, dout

  // Notes on the sheet:
  //   Matrix_A
  //   Matrix_B
endmodule

module counterdemo (
  input  in_1,
  input  in_2,
  input  in_3,
  input  in_4,
  input  [3:0] in_5,
  output [3:0] out_6
);

  Counter #(.max('h3), .ongoal("load"), .width(4)) counter_1 (
    .load(in_1), .up(in_2), .count(in_3), .clk(in_4), .D(in_5), .Q(out_6));  // open: clr, carry
endmodule

module assembly2 (
  input  OUTPUT_ENABLE,
  input  WE,
  input  OE,
  input  WRITE_ENABLE
);

  wire clock_1_out, Delay_Counter_carry;
  wire [4:0] counter_1_q;
  wire [63:0] matrixadder2x2core_1_r11, matrixadder2x2core_1_r12, matrixadder2x2core_1_r21,
       matrixadder2x2core_1_r22, R_11_dout, R_12_dout, R_21_dout, R_22_dout, RAM_A11_dout, RAM_A12_dout,
       RAM_A21_dout, RAM_A22_dout, RAM_B11_dout, RAM_B12_dout, RAM_B21_dout, RAM_B22_dout;

  Clock clock_1 (.out(clock_1_out));
  RAM #(.addrWidth(5), .dataWidth(64), .\type ("nonvolatile")) RAM_A11 (
    .addr(counter_1_q), .we(WE), .oe(1'b1), .clk(clock_1_out), .din(R_11_dout), .dout(RAM_A11_dout));
  // Probe on RAM_B12_dout
  Counter #(.max('h2), .width(4)) Delay_Counter (
    .count(clock_1_out), .clk(clock_1_out), .carry(Delay_Counter_carry));  // open: clr, load, up, D, Q
  // Probe on RAM_A12_dout
  // Probe on RAM_A11_dout
  RAM #(.addrWidth(5), .dataWidth(64), .\type ("nonvolatile")) RAM_A12 (
    .addr(counter_1_q), .oe(1'b1), .clk(clock_1_out), .din(R_21_dout), .dout(RAM_A12_dout));  // open: we
  Counter #(.max('h7), .width(5)) counter_1 (
    .count(Delay_Counter_carry), .clk(clock_1_out), .Q(counter_1_q));  // open: clr, load, up, D, carry
  matrixAdder2x2Core matrixadder2x2core_1 (
    .A11(RAM_A11_dout), .A12(RAM_A12_dout), .A21(RAM_A21_dout), .A22(RAM_A22_dout), .B11(RAM_B11_dout),
    .B12(RAM_B12_dout), .B21(RAM_B21_dout), .B22(RAM_B22_dout), .R11(matrixadder2x2core_1_r11),
    .R12(matrixadder2x2core_1_r12), .R21(matrixadder2x2core_1_r21), .R22(matrixadder2x2core_1_r22));
  RAM #(.addrWidth(5), .dataWidth(64), .\type ("nonvolatile")) RAM_A21 (
    .addr(counter_1_q), .we(WE), .oe(1'b1), .clk(clock_1_out), .dout(RAM_A21_dout));  // open: din
  // Probe on matrixadder2x2core_1_r11
  // Probe on matrixadder2x2core_1_r12
  RAM #(.addrWidth(5), .dataWidth(64), .\type ("nonvolatile")) RAM_A22 (
    .addr(counter_1_q), .we(WE), .oe(1'b1), .clk(clock_1_out), .dout(RAM_A22_dout));  // open: din
  RAM #(.addrWidth(5), .dataWidth(64)) R_11 (
    .addr(counter_1_q), .we(1'b1), .oe(OE), .clk(clock_1_out), .din(matrixadder2x2core_1_r11),
    .dout(R_11_dout));
  // Probe on matrixadder2x2core_1_r21
  RAM #(.addrWidth(5), .dataWidth(64), .\type ("nonvolatile")) RAM_B11 (
    .addr(counter_1_q), .we(WE), .oe(1'b1), .clk(clock_1_out), .din(R_12_dout), .dout(RAM_B11_dout));
  // Probe on matrixadder2x2core_1_r12
  RAM #(.addrWidth(5), .dataWidth(64), .\type ("nonvolatile")) RAM_B12 (
    .addr(counter_1_q), .we(WE), .oe(1'b1), .clk(clock_1_out), .din(R_22_dout), .dout(RAM_B12_dout));
  RAM #(.addrWidth(5), .dataWidth(64)) R_12 (
    .addr(counter_1_q), .we(1'b1), .oe(OE), .clk(clock_1_out), .din(matrixadder2x2core_1_r12),
    .dout(R_12_dout));
  RAM #(.addrWidth(5), .dataWidth(64), .\type ("nonvolatile")) RAM_B21 (
    .addr(counter_1_q), .we(WE), .oe(1'b1), .clk(clock_1_out), .dout(RAM_B21_dout));  // open: din
  RAM #(.addrWidth(5), .dataWidth(64)) R_21 (
    .addr(counter_1_q), .we(1'b1), .oe(OE), .clk(clock_1_out), .din(matrixadder2x2core_1_r22),
    .dout(R_21_dout));
  RAM #(.addrWidth(5), .dataWidth(64), .\type ("nonvolatile")) RAM_B22 (
    .addr(counter_1_q), .we(WE), .oe(1'b1), .clk(clock_1_out), .dout(RAM_B22_dout));  // open: din
  RAM #(.addrWidth(5), .dataWidth(64)) R_22 (
    .addr(counter_1_q), .we(1'b1), .oe(OE), .clk(clock_1_out), .din(matrixadder2x2core_1_r21),
    .dout(R_22_dout));

  // Notes on the sheet:
  //   Matrix_A
  //   Matrix_B
endmodule

module test_assembly (
  input  OUTPUT_ENABLE,
  input  WE,
  input  OE,
  input  WRITE_ENABLE
);

  wire clock_1_out, Delay_Counter_carry;
  wire [4:0] counter_1_q, counter_2_q;
  wire [63:0] matrixadder2x2core_1_r11, matrixadder2x2core_1_r12, matrixadder2x2core_1_r21,
       matrixadder2x2core_1_r22, R_11_dout, R_12_dout, R_21_dout, R_22_dout, RAM_A11_dout, RAM_A12_dout,
       RAM_A21_dout, RAM_A22_dout, RAM_B11_dout, RAM_B12_dout, RAM_B21_dout, RAM_B22_dout;

  Clock clock_1 (.out(clock_1_out));
  RAM #(.addrWidth(5), .dataWidth(64), .\type ("nonvolatile")) RAM_A11 (
    .addr(counter_2_q), .we(WE), .oe(1'b1), .clk(clock_1_out), .din(R_11_dout), .dout(RAM_A11_dout));
  // Probe on RAM_B12_dout
  Counter #(.max('h2), .width(4)) Delay_Counter (
    .count(clock_1_out), .clk(clock_1_out), .carry(Delay_Counter_carry));  // open: clr, load, up, D, Q
  // Probe on RAM_A12_dout
  // Probe on RAM_A11_dout
  Counter #(.max('h7), .width(5)) counter_1 (
    .clk(clock_1_out), .Q(counter_1_q));  // open: clr, load, up, count, D, carry
  RAM #(.addrWidth(5), .dataWidth(64), .\type ("nonvolatile")) RAM_A12 (
    .addr(counter_2_q), .oe(1'b1), .clk(clock_1_out), .din(R_21_dout), .dout(RAM_A12_dout));  // open: we
  Counter #(.max('h18), .width(5)) counter_2 (
    .count(Delay_Counter_carry), .clk(clock_1_out), .Q(counter_2_q));  // open: clr, load, up, D, carry
  matrixAdder2x2Core matrixadder2x2core_1 (
    .A11(RAM_A11_dout), .A12(RAM_A12_dout), .A21(RAM_A21_dout), .A22(RAM_A22_dout), .B11(RAM_B11_dout),
    .B12(RAM_B12_dout), .B21(RAM_B21_dout), .B22(RAM_B22_dout), .R11(matrixadder2x2core_1_r11),
    .R12(matrixadder2x2core_1_r12), .R21(matrixadder2x2core_1_r21), .R22(matrixadder2x2core_1_r22));
  RAM #(.addrWidth(5), .dataWidth(64), .\type ("nonvolatile")) RAM_A21 (
    .addr(counter_2_q), .we(WE), .oe(1'b1), .clk(clock_1_out), .dout(RAM_A21_dout));  // open: din
  // Probe on matrixadder2x2core_1_r11
  // Probe on matrixadder2x2core_1_r12
  RAM #(.addrWidth(5), .dataWidth(64), .\type ("nonvolatile")) RAM_A22 (
    .addr(counter_2_q), .we(WE), .oe(1'b1), .clk(clock_1_out), .dout(RAM_A22_dout));  // open: din
  RAM #(.addrWidth(5), .dataWidth(64)) R_11 (
    .addr(counter_1_q), .we(1'b1), .oe(OE), .clk(clock_1_out), .din(matrixadder2x2core_1_r11),
    .dout(R_11_dout));
  // Probe on matrixadder2x2core_1_r21
  RAM #(.addrWidth(5), .dataWidth(64), .\type ("nonvolatile")) RAM_B11 (
    .addr(counter_2_q), .we(WE), .oe(1'b1), .clk(clock_1_out), .din(R_12_dout), .dout(RAM_B11_dout));
  // Probe on matrixadder2x2core_1_r12
  RAM #(.addrWidth(5), .dataWidth(64), .\type ("nonvolatile")) RAM_B12 (
    .addr(counter_2_q), .we(WE), .oe(1'b1), .clk(clock_1_out), .din(R_22_dout), .dout(RAM_B12_dout));
  RAM #(.addrWidth(5), .dataWidth(64)) R_12 (
    .addr(counter_1_q), .we(1'b1), .oe(OE), .clk(clock_1_out), .din(matrixadder2x2core_1_r12),
    .dout(R_12_dout));
  RAM #(.addrWidth(5), .dataWidth(64), .\type ("nonvolatile")) RAM_B21 (
    .addr(counter_2_q), .we(WE), .oe(1'b1), .clk(clock_1_out), .dout(RAM_B21_dout));  // open: din
  RAM #(.addrWidth(5), .dataWidth(64)) R_21 (
    .addr(counter_1_q), .we(1'b1), .oe(OE), .clk(clock_1_out), .din(matrixadder2x2core_1_r22),
    .dout(R_21_dout));
  RAM #(.addrWidth(5), .dataWidth(64), .\type ("nonvolatile")) RAM_B22 (
    .addr(counter_2_q), .we(WE), .oe(1'b1), .clk(clock_1_out), .dout(RAM_B22_dout));  // open: din
  RAM #(.addrWidth(5), .dataWidth(64)) R_22 (
    .addr(counter_1_q), .we(1'b1), .oe(OE), .clk(clock_1_out), .din(matrixadder2x2core_1_r21),
    .dout(R_22_dout));

  // Notes on the sheet:
  //   Matrix_A
  //   Matrix_B
endmodule

module multiplier_Core (
  input  [63:0] A11,
  input  [63:0] B11,
  input  [63:0] A12,
  input  [63:0] B12,
  input  [63:0] A21,
  input  [63:0] B21,
  input  [63:0] A22,
  input  [63:0] B22,
  output [63:0] R11,
  output [63:0] xtra64bits,
  output [63:0] R12,
  output [63:0] xtra64bits2,
  output [63:0] R21,
  output [63:0] xtra64bits3,
  output [63:0] R22,
  output [63:0] xtra64bits4
);

  // Probe on A11
  // Probe on A12
  // Probe on A21
  // Probe on A22
  // Probe on B11
  // Probe on B12
  // Probe on B21
  // Probe on B22
  Multiplier #(.width(64)) multiplier_1 (.a(A11), .b(B11), .out(R11), .cout(xtra64bits));  // open: cin
  Multiplier #(.width(64)) multiplier_2 (.a(A12), .b(B12), .out(R12), .cout(xtra64bits2));  // open: cin
  Multiplier #(.width(64)) multiplier_3 (.a(A21), .b(B21), .out(R21), .cout(xtra64bits3));  // open: cin
  Multiplier #(.width(64)) multiplier_4 (.a(A22), .b(B22), .out(R22), .cout(xtra64bits4));  // open: cin
  // Probe on R11
  // Probe on R12
  // Probe on R21
  // Probe on R22
endmodule

module mat_mult_node (
  input  [63:0] A11,
  input  [63:0] A12,
  input  [63:0] A21,
  input  [63:0] A22,
  input  [63:0] B11,
  input  [63:0] B12,
  input  [63:0] B21,
  input  [63:0] B22,
  output [63:0] R11,
  output [63:0] R12,
  output [63:0] R21,
  output [63:0] R22
);

  wire [63:0] multiplier_1_out, multiplier_2_out, multiplier_3_out, multiplier_4_out, multiplier_5_out,
       multiplier_6_out, multiplier_7_out, multiplier_8_out;

  // Probe on A12
  // Probe on B11
  // Probe on B21
  // Probe on A11
  // Probe on A21
  // Probe on B11
  Multiplier #(.width(64)) multiplier_1 (.a(A11), .b(B11), .out(multiplier_1_out));  // open: cin, cout
  Multiplier #(.width(64)) multiplier_2 (.a(A12), .b(B21), .out(multiplier_2_out));  // open: cin, cout
  Multiplier #(.width(64)) multiplier_3 (.a(A11), .b(B12), .out(multiplier_3_out));  // open: cin, cout
  Multiplier #(.width(64)) multiplier_4 (.a(A12), .b(B22), .out(multiplier_4_out));  // open: cin, cout
  Multiplier #(.width(64)) multiplier_5 (.a(A21), .b(B11), .out(multiplier_5_out));  // open: cin, cout
  Multiplier #(.width(64)) multiplier_6 (.a(A22), .b(B21), .out(multiplier_6_out));  // open: cin, cout
  Multiplier #(.width(64)) multiplier_7 (.a(A21), .b(B12), .out(multiplier_7_out));  // open: cin, cout
  Multiplier #(.width(64)) multiplier_8 (.a(A22), .b(B22), .out(multiplier_8_out));  // open: cin, cout
  // Probe on multiplier_1_out
  // Probe on multiplier_3_out
  // Probe on multiplier_7_out
  // Probe on multiplier_2_out
  // Probe on multiplier_4_out
  // Probe on multiplier_5_out
  // Probe on multiplier_6_out
  // Probe on multiplier_8_out
  sixtyFour_bit_Adder sixtyfour_bit_adder_1 (
    .A(multiplier_1_out), .B(multiplier_2_out), .sum_out(R11));  // open: cin, cout
  sixtyFour_bit_Adder sixtyfour_bit_adder_2 (
    .A(multiplier_3_out), .B(multiplier_4_out), .sum_out(R12));  // open: cin, cout
  sixtyFour_bit_Adder sixtyfour_bit_adder_3 (
    .A(multiplier_5_out), .B(multiplier_6_out), .sum_out(R21));  // open: cin, cout
  sixtyFour_bit_Adder sixtyfour_bit_adder_4 (
    .A(multiplier_7_out), .B(multiplier_8_out), .sum_out(R22));  // open: cin, cout
  // Probe on R11
  // Probe on R12
  // Probe on R21
  // Probe on R22
endmodule

module Assembly_With_MatMult (
  input  OUTPUT_ENABLE,
  input  write_ENNBLE,
  input  WRITE_ENABLE
);

  wire clock_1_out, Delay_Counter_carry;
  wire [3:0] counter_1_q;
  wire [63:0] mat_mult_node_1_r11, mat_mult_node_1_r12, mat_mult_node_1_r21, mat_mult_node_1_r22, R_11_dout,
       RAM_A11_dout, RAM_A12_dout, RAM_A21_dout, RAM_A22_dout, RAM_B11_dout, RAM_B12_dout, RAM_B21_dout,
       RAM_B22_dout, undriven;

  Clock clock_1 (.out(clock_1_out));
  RAM #(.addrWidth(4), .dataWidth(64), .\type ("nonvolatile")) RAM_A11 (
    .addr(counter_1_q), .we(write_ENNBLE), .oe(1'b1), .clk(clock_1_out), .dout(RAM_A11_dout));  // open: din
  // Probe on RAM_A21_dout
  // Probe on RAM_B21_dout
  Counter #(.max('h2), .width(4)) Delay_Counter (
    .count(clock_1_out), .clk(clock_1_out), .carry(Delay_Counter_carry));  // open: clr, load, up, D, Q
  // Probe on RAM_A11_dout
  RAM #(.addrWidth(4), .dataWidth(64), .\type ("nonvolatile")) RAM_A12 (
    .addr(counter_1_q), .we(write_ENNBLE), .clk(clock_1_out), .dout(RAM_A12_dout));  // open: oe, din
  Counter #(.max('h7), .width(4)) counter_1 (
    .count(Delay_Counter_carry), .clk(clock_1_out), .Q(counter_1_q));  // open: clr, load, up, D, carry
  mat_mult_node mat_mult_node_1 (
    .A11(RAM_A11_dout), .A12(RAM_A12_dout), .A21(RAM_A21_dout), .A22(RAM_A22_dout), .B11(RAM_B11_dout),
    .B12(RAM_B12_dout), .B21(RAM_B21_dout), .B22(RAM_B22_dout), .R11(mat_mult_node_1_r11),
    .R12(mat_mult_node_1_r12), .R21(mat_mult_node_1_r21), .R22(mat_mult_node_1_r22));
  RAM #(.addrWidth(4), .dataWidth(64), .\type ("nonvolatile")) RAM_A21 (
    .addr(counter_1_q), .we(write_ENNBLE), .oe(1'b1), .clk(clock_1_out), .dout(RAM_A21_dout));  // open: din
  // Probe on mat_mult_node_1_r11
  // Probe on mat_mult_node_1_r12
  RAM #(.addrWidth(4), .dataWidth(64), .\type ("nonvolatile")) RAM_A22 (
    .addr(counter_1_q), .we(write_ENNBLE), .oe(1'b1), .clk(clock_1_out), .dout(RAM_A22_dout));  // open: din
  RAM #(.addrWidth(4), .dataWidth(64)) R_11 (
    .addr(counter_1_q), .we(1'b1), .clk(clock_1_out), .din(mat_mult_node_1_r11), .dout(R_11_dout));  // open: oe
  // Probe on mat_mult_node_1_r21
  RAM #(.addrWidth(4), .dataWidth(64), .\type ("nonvolatile")) RAM_B11 (
    .addr(counter_1_q), .we(write_ENNBLE), .oe(1'b1), .clk(clock_1_out), .din(undriven), .dout(RAM_B11_dout));
  // Probe on mat_mult_node_1_r22
  RAM #(.addrWidth(4), .dataWidth(64), .\type ("nonvolatile")) RAM_B12 (
    .addr(counter_1_q), .we(write_ENNBLE), .oe(1'b1), .clk(clock_1_out), .dout(RAM_B12_dout));  // open: din
  RAM #(.addrWidth(4), .dataWidth(64)) R_12 (
    .addr(counter_1_q), .we(1'b1), .clk(clock_1_out), .din(mat_mult_node_1_r12));  // open: oe, dout
  RAM #(.addrWidth(4), .dataWidth(64), .\type ("nonvolatile")) RAM_B21 (
    .addr(counter_1_q), .we(write_ENNBLE), .oe(1'b1), .clk(clock_1_out), .dout(RAM_B21_dout));  // open: din
  // Probe on mat_mult_node_1_r22
  RAM #(.addrWidth(4), .dataWidth(64)) R_21 (
    .addr(counter_1_q), .we(1'b1), .clk(clock_1_out), .din(mat_mult_node_1_r22));  // open: oe, dout
  RAM #(.addrWidth(4), .dataWidth(64), .\type ("nonvolatile")) RAM_B22 (
    .addr(counter_1_q), .we(write_ENNBLE), .oe(1'b1), .clk(clock_1_out), .dout(RAM_B22_dout));  // open: din
  RAM #(.addrWidth(4), .dataWidth(64)) R_22 (
    .addr(counter_1_q), .we(1'b1), .clk(clock_1_out), .din(mat_mult_node_1_r21));  // open: oe, dout

  // Notes on the sheet:
  //   Matrix_A
  //   Matrix_B
endmodule

module debugger_or_sumshi (
  input  [1:0] in_1,
  output ioe,
  output owe,
  output ooe,
  output iwe
);

  wire not_1_out;

  not not_1 (not_1_out, in_1[1]);
  and and_1 (ioe, ~in_1[0], ~in_1[1]);  // AND_Gate
  and and_2 (owe, in_1[0], not_1_out);
  and and_3 (ooe, ~in_1[0], in_1[1]);  // AND_Gate
  and and_4 (iwe, in_1[0], in_1[1]);
endmodule

module mat_mult_4x4 (
  input  [63:0] A11_11,
  input  [63:0] A11_12,
  input  [63:0] A11_21,
  input  [63:0] A11_22,
  input  [63:0] A12_11,
  input  [63:0] A12_12,
  input  [63:0] A12_21,
  input  [63:0] A12_22,
  input  [63:0] B11_11,
  input  [63:0] B11_12,
  input  [63:0] B11_21,
  input  [63:0] B11_22,
  input  [63:0] B21_11,
  input  [63:0] B21_12,
  input  [63:0] B21_21,
  input  [63:0] B21_22,
  output [63:0] R11,
  output [63:0] R12,
  output [63:0] R21,
  output [63:0] R22
);

  wire [63:0] mat_mult_node_1_r11, mat_mult_node_1_r12, mat_mult_node_1_r21, mat_mult_node_1_r22,
       mat_mult_node_2_r11, mat_mult_node_2_r12, mat_mult_node_2_r21, mat_mult_node_2_r22;

  // Probe on B11_12
  // Probe on B11_11
  // Probe on B21_11
  // Probe on B21_12
  // Probe on B21_21
  // Probe on B11_21
  // Probe on B21_22
  // Probe on A11_11
  // Probe on B11_22
  // Probe on A11_12
  // Probe on A12_11
  // Probe on A11_21
  // Probe on A12_12
  // Probe on A11_22
  // Probe on A12_21
  // Probe on A12_22
  // Probe on mat_mult_node_1_r22
  // Probe on mat_mult_node_1_r21
  // Probe on mat_mult_node_1_r12
  // Probe on mat_mult_node_1_r11
  mat_mult_node mat_mult_node_1 (
    .A11(A12_11), .A12(A12_12), .A21(A12_21), .A22(A12_22), .B11(B21_11), .B12(B21_12), .B21(B21_21),
    .B22(B21_22), .R11(mat_mult_node_1_r11), .R12(mat_mult_node_1_r12), .R21(mat_mult_node_1_r21),
    .R22(mat_mult_node_1_r22));
  // Probe on mat_mult_node_2_r11
  mat_mult_node mat_mult_node_2 (
    .A11(A11_11), .A12(A11_12), .A21(A11_21), .A22(A11_22), .B11(B11_11), .B12(B11_12), .B21(B11_21),
    .B22(B11_22), .R11(mat_mult_node_2_r11), .R12(mat_mult_node_2_r12), .R21(mat_mult_node_2_r21),
    .R22(mat_mult_node_2_r22));
  // Probe on mat_mult_node_2_r12
  // Probe on mat_mult_node_2_r22
  // Probe on mat_mult_node_2_r21
  // Probe on R21
  // Probe on R12
  // Probe on R11
  matrixAdder2x2Core matrixadder2x2core_1 (
    .A11(mat_mult_node_2_r11), .A12(mat_mult_node_2_r12), .A21(mat_mult_node_2_r21),
    .A22(mat_mult_node_2_r22), .B11(mat_mult_node_1_r11), .B12(mat_mult_node_1_r12),
    .B21(mat_mult_node_1_r21), .B22(mat_mult_node_1_r22), .R11(R11), .R12(R12), .R21(R21), .R22(R22));
  // Probe on R22

  // Notes on the sheet:
  //   A11
  //   A12
  //   B11
  //   B21
endmodule

module Assembly_4x4_mat_mult (
);

  wire clock_1_out, counter_1_carry, counter_2_carry, counter_3_carry;
  wire [3:0] counter_3_q, counter_4_q, counter_5_q;
  wire [63:0] A11_11_dout, A11_12_dout, A11_21_dout, A11_22_dout, A12_11_dout, A12_12_dout, A12_21_dout,
       A12_22_dout, B11_11_dout, B11_12_dout, B11_21_dout, B11_22_dout, B12_11_dout, B12_12_dout,
       B12_21_dout, B12_22_dout, mat_mult_4x4_1_r11, mat_mult_4x4_1_r12, mat_mult_4x4_1_r21,
       mat_mult_4x4_1_r22;

  RAM #(.addrWidth(4), .dataWidth(64), .\type ("nonvolatile")) B11_11 (
    .addr(counter_3_q), .oe(1'b1), .clk(clock_1_out), .dout(B11_11_dout));  // open: we, din
  RAM #(.addrWidth(4), .dataWidth(64), .\type ("nonvolatile")) B11_12 (
    .addr(counter_3_q), .oe(1'b1), .clk(clock_1_out), .dout(B11_12_dout));  // open: we, din
  // Probe on B11_11_dout
  // Probe on B11_12_dout
  RAM #(.addrWidth(4), .dataWidth(64), .\type ("nonvolatile")) B11_21 (
    .addr(counter_3_q), .oe(1'b1), .clk(clock_1_out), .dout(B11_21_dout));  // open: we, din
  RAM #(.addrWidth(4), .dataWidth(64), .\type ("nonvolatile")) B11_22 (
    .addr(counter_3_q), .oe(1'b1), .clk(clock_1_out), .dout(B11_22_dout));  // open: we, din
  // Probe on B11_21_dout
  // Probe on B11_22_dout
  RAM #(.addrWidth(4), .dataWidth(64), .\type ("nonvolatile")) B12_11 (
    .addr(counter_3_q), .oe(1'b1), .clk(clock_1_out), .dout(B12_11_dout));  // open: we, din
  RAM #(.addrWidth(4), .dataWidth(64), .\type ("nonvolatile")) B12_12 (
    .addr(counter_3_q), .oe(1'b1), .clk(clock_1_out), .dout(B12_12_dout));  // open: we, din
  // Probe on B12_11_dout
  // Probe on B12_12_dout
  RAM #(.addrWidth(4), .dataWidth(64), .\type ("nonvolatile")) B12_21 (
    .addr(counter_3_q), .oe(1'b1), .clk(clock_1_out), .dout(B12_21_dout));  // open: we, din
  RAM #(.addrWidth(4), .dataWidth(64), .\type ("nonvolatile")) B12_22 (
    .addr(counter_3_q), .oe(1'b1), .clk(clock_1_out), .dout(B12_22_dout));  // open: we, din
  Counter #(.max('h1), .width(2)) counter_1 (
    .count(clock_1_out), .clk(clock_1_out), .carry(counter_1_carry));  // open: clr, load, up, D, Q
  // Probe on B12_22_dout
  Counter #(.max('h1), .width(1)) counter_2 (
    .clk(clock_1_out), .carry(counter_2_carry));  // open: clr, load, up, count, D, Q
  // Probe on B12_21_dout
  Counter #(.max('h1), .width(4)) counter_3 (
    .count(counter_1_carry), .clk(clock_1_out), .carry(counter_3_carry), .Q(counter_3_q));  // open: clr, load, up, D
  Counter #(.max('h1), .ongoal("stay"), .width(4)) counter_4 (
    .count(counter_3_carry), .clk(clock_1_out), .Q(counter_4_q));  // open: clr, load, up, D, carry
  // Probe on B11_11_dout
  Counter #(.max('h3), .width(4)) counter_5 (
    .count(counter_2_carry), .clk(clock_1_out), .Q(counter_5_q));  // open: clr, load, up, D, carry
  Clock clock_1 (.out(clock_1_out));
  // Probe on mat_mult_4x4_1_r22
  // Probe on mat_mult_4x4_1_r21
  // Probe on mat_mult_4x4_1_r12
  // Probe on mat_mult_4x4_1_r11
  mat_mult_4x4 mat_mult_4x4_1 (
    .A11_11(A11_11_dout), .A11_12(A11_12_dout), .A11_21(A11_21_dout), .A11_22(A11_22_dout),
    .A12_11(A12_11_dout), .A12_12(A12_12_dout), .A12_21(A12_21_dout), .A12_22(A12_22_dout),
    .B11_11(B11_11_dout), .B11_12(B11_12_dout), .B11_21(B11_21_dout), .B11_22(B11_22_dout),
    .B21_11(B12_11_dout), .B21_12(B12_12_dout), .B21_21(B12_21_dout), .B21_22(B12_22_dout),
    .R11(mat_mult_4x4_1_r11), .R12(mat_mult_4x4_1_r12), .R21(mat_mult_4x4_1_r21), .R22(mat_mult_4x4_1_r22));
  // Probe on A11_11_dout
  RAM #(.addrWidth(4), .dataWidth(64), .\type ("nonvolatile")) A11_11 (
    .addr(counter_4_q), .oe(1'b1), .clk(clock_1_out), .dout(A11_11_dout));  // open: we, din
  RAM #(.addrWidth(4), .dataWidth(64), .\type ("nonvolatile")) A11_12 (
    .addr(counter_4_q), .oe(1'b1), .clk(clock_1_out), .dout(A11_12_dout));  // open: we, din
  RAM #(.addrWidth(4), .dataWidth(64)) ram_1 (
    .addr(counter_5_q), .we(1'b1), .clk(clock_1_out), .din(mat_mult_4x4_1_r11));  // open: oe, dout
  // Probe on A11_11_dout
  // Probe on A11_12_dout
  RAM #(.addrWidth(4), .dataWidth(64), .\type ("nonvolatile")) A11_21 (
    .addr(counter_4_q), .oe(1'b1), .clk(clock_1_out), .dout(A11_21_dout));  // open: we, din
  RAM #(.addrWidth(4), .dataWidth(64), .\type ("nonvolatile")) A11_22 (
    .addr(counter_4_q), .oe(1'b1), .clk(clock_1_out), .dout(A11_22_dout));  // open: we, din
  RAM #(.addrWidth(4), .dataWidth(64)) ram_2 (
    .addr(counter_5_q), .we(1'b1), .clk(clock_1_out), .din(mat_mult_4x4_1_r12));  // open: oe, dout
  // Probe on A11_21_dout
  // Probe on A11_22_dout
  RAM #(.addrWidth(4), .dataWidth(64), .\type ("nonvolatile")) A12_11 (
    .addr(counter_4_q), .oe(1'b1), .clk(clock_1_out), .dout(A12_11_dout));  // open: we, din
  RAM #(.addrWidth(4), .dataWidth(64), .\type ("nonvolatile")) A12_12 (
    .addr(counter_4_q), .oe(1'b1), .clk(clock_1_out), .dout(A12_12_dout));  // open: we, din
  RAM #(.addrWidth(4), .dataWidth(64)) ram_3 (
    .addr(counter_5_q), .we(1'b1), .clk(clock_1_out), .din(mat_mult_4x4_1_r21));  // open: oe, dout
  // Probe on A12_11_dout
  // Probe on A12_12_dout
  RAM #(.addrWidth(4), .dataWidth(64), .\type ("nonvolatile")) A12_21 (
    .addr(counter_4_q), .oe(1'b1), .clk(clock_1_out), .dout(A12_21_dout));  // open: we, din
  RAM #(.addrWidth(4), .dataWidth(64), .\type ("nonvolatile")) A12_22 (
    .addr(counter_4_q), .oe(1'b1), .clk(clock_1_out), .dout(A12_22_dout));  // open: we, din
  RAM #(.addrWidth(4), .dataWidth(64)) ram_4 (
    .addr(counter_5_q), .we(1'b1), .clk(clock_1_out), .din(mat_mult_4x4_1_r22));  // open: oe, dout
  // Probe on A12_21_dout
  // Probe on A12_22_dout
endmodule

module matrixAdder4x4 (
  input  [63:0] A11_11,
  input  [63:0] A11_12,
  input  [63:0] A11_21,
  input  [63:0] A11_22,
  input  [63:0] A12_11,
  input  [63:0] A12_12,
  input  [63:0] A12_21,
  input  [63:0] A12_22,
  input  [63:0] A21_11,
  input  [63:0] A21_12,
  input  [63:0] A21_21,
  input  [63:0] A21_22,
  input  [63:0] A22_11,
  input  [63:0] A22_12,
  input  [63:0] A22_21,
  input  [63:0] A22_22,
  input  [63:0] B11_11,
  input  [63:0] B11_12,
  input  [63:0] B11_21,
  input  [63:0] B11_22,
  input  [63:0] B12_11,
  input  [63:0] B12_12,
  input  [63:0] B12_21,
  input  [63:0] B12_22,
  input  [63:0] B21_11,
  input  [63:0] B21_12,
  input  [63:0] B21_21,
  input  [63:0] B21_22,
  input  [63:0] B22_11,
  input  [63:0] B22_12,
  input  [63:0] B22_21,
  input  [63:0] B22_22,
  output [63:0] R11_11,
  output [63:0] R11_12,
  output [63:0] R11_21,
  output [63:0] R11_22,
  output [63:0] R12_11,
  output [63:0] R12_12,
  output [63:0] R12_21,
  output [63:0] R12_22,
  output [63:0] R21_11,
  output [63:0] R21_12,
  output [63:0] R21_21,
  output [63:0] R21_22,
  output [63:0] R22_11,
  output [63:0] R22_12,
  output [63:0] R22_21,
  output [63:0] R22_22
);

  matrixAdder2x2Core matrixadder2x2core_1 (
    .A11(A11_11), .A12(A11_12), .A21(A11_21), .A22(A11_22), .B11(B11_11), .B12(B11_12), .B21(B11_21),
    .B22(B11_22), .R11(R11_11), .R12(R11_12), .R21(R11_21), .R22(R11_22));
  matrixAdder2x2Core matrixadder2x2core_2 (
    .A11(A12_11), .A12(A12_12), .A21(A12_21), .A22(A12_22), .B11(B12_11), .B12(B12_12), .B21(B12_21),
    .B22(B12_22), .R11(R12_11), .R12(R12_12), .R21(R12_21), .R22(R12_22));
  matrixAdder2x2Core matrixadder2x2core_3 (
    .A11(A21_11), .A12(A21_12), .A21(A21_21), .A22(A21_22), .B11(B21_11), .B12(B21_12), .B21(B21_21),
    .B22(B21_22), .R11(R21_11), .R12(R21_12), .R21(R21_21), .R22(R21_22));
  matrixAdder2x2Core matrixadder2x2core_4 (
    .A11(A22_11), .A12(A22_12), .A21(A22_21), .A22(A22_22), .B11(B22_11), .B12(B22_12), .B21(B22_21),
    .B22(B22_22), .R11(R22_11), .R12(R22_12), .R21(R22_21), .R22(R22_22));
endmodule

module core_8x8 (
  input  [63:0] A11_11,
  input  [63:0] A11_12,
  input  [63:0] A11_21,
  input  [63:0] A11_22,
  input  [63:0] A12_11,
  input  [63:0] A12_12,
  input  [63:0] A12_21,
  input  [63:0] A12_22,
  input  [63:0] A13_11,
  input  [63:0] A13_12,
  input  [63:0] A13_21,
  input  [63:0] A13_22,
  input  [63:0] A14_11,
  input  [63:0] A14_12,
  input  [63:0] A14_21,
  input  [63:0] A14_22,
  input  [63:0] B11_11,
  input  [63:0] B11_12,
  input  [63:0] B11_21,
  input  [63:0] B11_22,
  input  [63:0] B21_11,
  input  [63:0] B21_12,
  input  [63:0] B21_21,
  input  [63:0] B21_22,
  input  [63:0] B31_11,
  input  [63:0] B31_12,
  input  [63:0] B31_21,
  input  [63:0] B31_22,
  input  [63:0] B41_11,
  input  [63:0] B41_12,
  input  [63:0] B41_21,
  input  [63:0] B41_22,
  output [63:0] R11,
  output [63:0] R12,
  output [63:0] R21,
  output [63:0] R22
);

  wire [63:0] mat_mult_node_1_r11, mat_mult_node_1_r12, mat_mult_node_1_r21, mat_mult_node_1_r22,
       mat_mult_node_2_r11, mat_mult_node_2_r12, mat_mult_node_2_r21, mat_mult_node_2_r22,
       mat_mult_node_3_r11, mat_mult_node_3_r12, mat_mult_node_3_r21, mat_mult_node_3_r22,
       mat_mult_node_4_r11, mat_mult_node_4_r12, mat_mult_node_4_r21, mat_mult_node_4_r22,
       matrixadder2x2core_1_r11, matrixadder2x2core_1_r12, matrixadder2x2core_1_r21,
       matrixadder2x2core_1_r22, matrixadder2x2core_2_r11, matrixadder2x2core_2_r12,
       matrixadder2x2core_2_r21, matrixadder2x2core_2_r22;

  mat_mult_node mat_mult_node_1 (
    .A11(A11_11), .A12(A11_12), .A21(A11_21), .A22(A11_22), .B11(B11_11), .B12(B11_12), .B21(B11_21),
    .B22(B11_22), .R11(mat_mult_node_1_r11), .R12(mat_mult_node_1_r12), .R21(mat_mult_node_1_r21),
    .R22(mat_mult_node_1_r22));
  mat_mult_node mat_mult_node_2 (
    .A11(A12_11), .A12(A12_12), .A21(A12_21), .A22(A12_22), .B11(B21_11), .B12(B21_12), .B21(B21_21),
    .B22(B21_22), .R11(mat_mult_node_2_r11), .R12(mat_mult_node_2_r12), .R21(mat_mult_node_2_r21),
    .R22(mat_mult_node_2_r22));
  mat_mult_node mat_mult_node_3 (
    .A11(A13_11), .A12(A13_12), .A21(A13_21), .A22(A13_22), .B11(B31_11), .B12(B31_12), .B21(B31_21),
    .B22(B31_22), .R11(mat_mult_node_3_r11), .R12(mat_mult_node_3_r12), .R21(mat_mult_node_3_r21),
    .R22(mat_mult_node_3_r22));
  mat_mult_node mat_mult_node_4 (
    .A11(A14_11), .A12(A14_12), .A21(A14_21), .A22(A14_22), .B11(B41_11), .B12(B41_12), .B21(B41_21),
    .B22(B41_22), .R11(mat_mult_node_4_r11), .R12(mat_mult_node_4_r12), .R21(mat_mult_node_4_r21),
    .R22(mat_mult_node_4_r22));
  matrixAdder2x2Core matrixadder2x2core_1 (
    .A11(mat_mult_node_1_r11), .A12(mat_mult_node_1_r12), .A21(mat_mult_node_1_r21),
    .A22(mat_mult_node_1_r22), .B11(mat_mult_node_2_r11), .B12(mat_mult_node_2_r12),
    .B21(mat_mult_node_2_r21), .B22(mat_mult_node_2_r22), .R11(matrixadder2x2core_1_r11),
    .R12(matrixadder2x2core_1_r12), .R21(matrixadder2x2core_1_r21), .R22(matrixadder2x2core_1_r22));
  matrixAdder2x2Core matrixadder2x2core_2 (
    .A11(mat_mult_node_3_r11), .A12(mat_mult_node_3_r12), .A21(mat_mult_node_3_r21),
    .A22(mat_mult_node_3_r22), .B11(mat_mult_node_4_r11), .B12(mat_mult_node_4_r12),
    .B21(mat_mult_node_4_r21), .B22(mat_mult_node_4_r22), .R11(matrixadder2x2core_2_r11),
    .R12(matrixadder2x2core_2_r12), .R21(matrixadder2x2core_2_r21), .R22(matrixadder2x2core_2_r22));
  matrixAdder2x2Core matrixadder2x2core_3 (
    .A11(matrixadder2x2core_1_r11), .A12(matrixadder2x2core_1_r12), .A21(matrixadder2x2core_1_r21),
    .A22(matrixadder2x2core_1_r22), .B11(matrixadder2x2core_2_r11), .B12(matrixadder2x2core_2_r12),
    .B21(matrixadder2x2core_2_r21), .B22(matrixadder2x2core_2_r22), .R11(R11), .R12(R12), .R21(R21), .R22(R22));

  // Notes on the sheet:
  //   A11
  //   A12
  //   A13
  //   A14
  //   B31
  //   B41
  //   B11
  //   B21
endmodule

module assembly_8x8 (
  input  in_1,
  input  [3:0] in_2,
  input  [3:0] in_3,
  input  in_4
);

  wire clock_1_out, counter_1_carry, counter_3_carry, Delay_counter_carry;
  wire [3:0] Address_Counter_A_q, counter_2_q, counter_4_q, multiplexer_1_out;
  wire [63:0] core_8x8_1_r11, core_8x8_1_r12, core_8x8_1_r21, core_8x8_1_r22, ram_1_dout, ram_2_dout,
       ram_3_dout, ram_4_dout, ram_5_dout, ram_6_dout, ram_7_dout, ram_8_dout, ram_9_dout, ram_10_dout,
       ram_11_dout, ram_12_dout, ram_13_dout, ram_14_dout, ram_15_dout, ram_16_dout, ram_17_dout,
       ram_18_dout, ram_19_dout, ram_20_dout, ram_23_dout, ram_24_dout, ram_25_dout, ram_26_dout,
       ram_29_dout, ram_30_dout, ram_31_dout, ram_32_dout, ram_33_dout, ram_34_dout, ram_35_dout, ram_36_dout;

  Multiplexer #(.width(4)) multiplexer_1 (.in0(in_2), .in1(in_3), .out(multiplexer_1_out), .sel(in_4));
  Counter #(.max('h1), .width(2)) Delay_counter (
    .count(clock_1_out), .clk(clock_1_out), .carry(Delay_counter_carry));  // open: clr, load, up, D, Q
  Counter #(.max('h4), .width(4)) Address_Counter_A (
    .up(in_1), .count(Delay_counter_carry), .clk(clock_1_out), .D(multiplexer_1_out), .Q(Address_Counter_A_q));  // open: clr, load, carry
  RAM #(.addrWidth(4), .dataWidth(64), .\type ("nonvolatile")) ram_1 (
    .addr(Address_Counter_A_q), .oe(1'b1), .clk(clock_1_out), .dout(ram_1_dout));  // open: we, din
  RAM #(.addrWidth(4), .dataWidth(64), .\type ("nonvolatile")) ram_2 (
    .addr(Address_Counter_A_q), .oe(1'b1), .clk(clock_1_out), .dout(ram_2_dout));  // open: we, din
  RAM #(.addrWidth(4), .dataWidth(64), .\type ("nonvolatile")) ram_3 (
    .addr(Address_Counter_A_q), .oe(1'b1), .clk(clock_1_out), .dout(ram_3_dout));  // open: we, din
  RAM #(.addrWidth(4), .dataWidth(64), .\type ("nonvolatile")) ram_4 (
    .addr(Address_Counter_A_q), .oe(1'b1), .clk(clock_1_out), .dout(ram_4_dout));  // open: we, din
  Clock clock_1 (.out(clock_1_out));
  RAM #(.addrWidth(4), .dataWidth(64), .\type ("nonvolatile")) ram_5 (
    .addr(Address_Counter_A_q), .clk(clock_1_out), .dout(ram_5_dout));  // open: we, oe, din
  RAM #(.addrWidth(4), .dataWidth(64), .\type ("nonvolatile")) ram_6 (
    .addr(Address_Counter_A_q), .clk(clock_1_out), .dout(ram_6_dout));  // open: we, oe, din
  RAM #(.addrWidth(4), .dataWidth(64), .\type ("nonvolatile")) ram_7 (
    .addr(Address_Counter_A_q), .clk(clock_1_out), .dout(ram_7_dout));  // open: we, oe, din
  RAM #(.addrWidth(4), .dataWidth(64), .\type ("nonvolatile")) ram_8 (
    .addr(Address_Counter_A_q), .clk(clock_1_out), .dout(ram_8_dout));  // open: we, oe, din
  RAM #(.addrWidth(4), .dataWidth(64), .\type ("nonvolatile")) ram_9 (
    .addr(Address_Counter_A_q), .clk(clock_1_out), .dout(ram_9_dout));  // open: we, oe, din
  RAM #(.addrWidth(4), .dataWidth(64), .\type ("nonvolatile")) ram_10 (
    .addr(Address_Counter_A_q), .clk(clock_1_out), .dout(ram_10_dout));  // open: we, oe, din
  RAM #(.addrWidth(4), .dataWidth(64), .\type ("nonvolatile")) ram_11 (
    .addr(Address_Counter_A_q), .clk(clock_1_out), .dout(ram_11_dout));  // open: we, oe, din
  RAM #(.addrWidth(4), .dataWidth(64), .\type ("nonvolatile")) ram_12 (
    .addr(Address_Counter_A_q), .clk(clock_1_out), .dout(ram_12_dout));  // open: we, oe, din
  RAM #(.addrWidth(4), .dataWidth(64), .\type ("nonvolatile")) ram_13 (
    .addr(Address_Counter_A_q), .clk(clock_1_out), .dout(ram_13_dout));  // open: we, oe, din
  RAM #(.addrWidth(4), .dataWidth(64), .\type ("nonvolatile")) ram_14 (
    .addr(Address_Counter_A_q), .clk(clock_1_out), .dout(ram_14_dout));  // open: we, oe, din
  RAM #(.addrWidth(4), .dataWidth(64), .\type ("nonvolatile")) ram_15 (
    .addr(Address_Counter_A_q), .clk(clock_1_out), .dout(ram_15_dout));  // open: we, oe, din
  RAM #(.addrWidth(4), .dataWidth(64), .\type ("nonvolatile")) ram_16 (
    .addr(Address_Counter_A_q), .clk(clock_1_out), .dout(ram_16_dout));  // open: we, oe, din
  Counter #(.max('h1), .width(2)) counter_1 (
    .count(clock_1_out), .clk(clock_1_out), .carry(counter_1_carry));  // open: clr, load, up, D, Q
  Counter #(.max('h4), .width(4)) counter_2 (
    .count(counter_1_carry), .clk(clock_1_out), .Q(counter_2_q));  // open: clr, load, up, D, carry
  RAM #(.addrWidth(4), .dataWidth(64), .\type ("nonvolatile")) ram_17 (
    .addr(counter_2_q), .oe(1'b1), .clk(clock_1_out), .dout(ram_17_dout));  // open: we, din
  RAM #(.addrWidth(4), .dataWidth(64), .\type ("nonvolatile")) ram_18 (
    .addr(counter_2_q), .oe(1'b1), .clk(clock_1_out), .dout(ram_18_dout));  // open: we, din
  RAM #(.addrWidth(4), .dataWidth(64), .\type ("nonvolatile")) ram_19 (
    .addr(counter_2_q), .oe(1'b1), .clk(clock_1_out), .dout(ram_19_dout));  // open: we, din
  RAM #(.addrWidth(4), .dataWidth(64), .\type ("nonvolatile")) ram_20 (
    .addr(counter_2_q), .oe(1'b1), .clk(clock_1_out), .dout(ram_20_dout));  // open: we, din
  Counter #(.max('h1), .width(1)) counter_3 (
    .count(clock_1_out), .clk(clock_1_out), .carry(counter_3_carry));  // open: clr, load, up, D, Q
  core_8x8 core_8x8_1 (
    .A11_11(ram_1_dout), .A11_12(ram_2_dout), .A11_21(ram_3_dout), .A11_22(ram_4_dout), .A12_11(ram_5_dout),
    .A12_12(ram_6_dout), .A12_21(ram_7_dout), .A12_22(ram_8_dout), .A13_11(ram_9_dout), .A13_12(ram_10_dout),
    .A13_21(ram_11_dout), .A13_22(ram_12_dout), .A14_11(ram_13_dout), .A14_12(ram_14_dout),
    .A14_21(ram_15_dout), .A14_22(ram_16_dout), .B11_11(ram_17_dout), .B11_12(ram_18_dout),
    .B11_21(ram_19_dout), .B11_22(ram_20_dout), .B21_11(ram_23_dout), .B21_12(ram_24_dout),
    .B21_21(ram_25_dout), .B21_22(ram_26_dout), .B31_11(ram_29_dout), .B31_12(ram_30_dout),
    .B31_21(ram_31_dout), .B31_22(ram_32_dout), .B41_11(ram_33_dout), .B41_12(ram_34_dout),
    .B41_21(ram_35_dout), .B41_22(ram_36_dout), .R11(core_8x8_1_r11), .R12(core_8x8_1_r12),
    .R21(core_8x8_1_r21), .R22(core_8x8_1_r22));
  Counter #(.max('h4), .width(4)) counter_4 (
    .count(counter_3_carry), .clk(clock_1_out), .Q(counter_4_q));  // open: clr, load, up, D, carry
  ROM #(.addrWidth(4), .dataWidth(64)) rom_1 ();  // open: addr, data
  RAM #(.addrWidth(4), .dataWidth(64), .\type ("nonvolatile")) ram_21 (
    .addr(counter_4_q), .we(1'b1), .clk(clock_1_out), .din(core_8x8_1_r11));  // open: oe, dout
  RAM #(.addrWidth(4), .dataWidth(64), .\type ("nonvolatile")) ram_22 (
    .addr(counter_4_q), .we(1'b1), .clk(clock_1_out), .din(core_8x8_1_r21));  // open: oe, dout
  RAM #(.addrWidth(4), .dataWidth(64), .\type ("nonvolatile")) ram_23 (
    .addr(counter_2_q), .clk(clock_1_out), .dout(ram_23_dout));  // open: we, oe, din
  RAM #(.addrWidth(4), .dataWidth(64), .\type ("nonvolatile")) ram_24 (
    .addr(counter_2_q), .clk(clock_1_out), .dout(ram_24_dout));  // open: we, oe, din
  RAM #(.addrWidth(4), .dataWidth(64), .\type ("nonvolatile")) ram_25 (
    .addr(counter_2_q), .clk(clock_1_out), .dout(ram_25_dout));  // open: we, oe, din
  RAM #(.addrWidth(4), .dataWidth(64), .\type ("nonvolatile")) ram_26 (
    .addr(counter_2_q), .clk(clock_1_out), .dout(ram_26_dout));  // open: we, oe, din
  RAM #(.addrWidth(4), .dataWidth(64), .\type ("nonvolatile")) ram_27 (
    .addr(counter_4_q), .we(1'b1), .clk(clock_1_out), .din(core_8x8_1_r12));  // open: oe, dout
  RAM #(.addrWidth(4), .dataWidth(64), .\type ("nonvolatile")) ram_28 (
    .addr(counter_4_q), .we(1'b1), .clk(clock_1_out), .din(core_8x8_1_r22));  // open: oe, dout
  RAM #(.addrWidth(4), .dataWidth(64), .\type ("nonvolatile")) ram_29 (
    .addr(counter_2_q), .clk(clock_1_out), .dout(ram_29_dout));  // open: we, oe, din
  RAM #(.addrWidth(4), .dataWidth(64), .\type ("nonvolatile")) ram_30 (
    .addr(counter_2_q), .clk(clock_1_out), .dout(ram_30_dout));  // open: we, oe, din
  RAM #(.addrWidth(4), .dataWidth(64), .\type ("nonvolatile")) ram_31 (
    .addr(counter_2_q), .clk(clock_1_out), .dout(ram_31_dout));  // open: we, oe, din
  RAM #(.addrWidth(4), .dataWidth(64), .\type ("nonvolatile")) ram_32 (
    .addr(counter_2_q), .clk(clock_1_out), .dout(ram_32_dout));  // open: we, oe, din
  RAM #(.addrWidth(4), .dataWidth(64), .\type ("nonvolatile")) ram_33 (
    .addr(counter_2_q), .clk(clock_1_out), .dout(ram_33_dout));  // open: we, oe, din
  RAM #(.addrWidth(4), .dataWidth(64), .\type ("nonvolatile")) ram_34 (
    .addr(counter_2_q), .clk(clock_1_out), .dout(ram_34_dout));  // open: we, oe, din
  RAM #(.addrWidth(4), .dataWidth(64), .\type ("nonvolatile")) ram_35 (
    .addr(counter_2_q), .clk(clock_1_out), .dout(ram_35_dout));  // open: we, oe, din
  RAM #(.addrWidth(4), .dataWidth(64), .\type ("nonvolatile")) ram_36 (
    .addr(counter_2_q), .clk(clock_1_out), .dout(ram_36_dout));  // open: we, oe, din

  // Notes on the sheet:
  //   A11
  //   A12
  //   A13
  //   A14
  //   B11
  //   B21
  //   B31
  //   B41
endmodule

module assembly_8x8_working (
);

  wire Address_Counter_A_carry, and_1_out, and_2_out, clock_1_out, counter_2_carry, register_2_q;
  wire [3:0] adder_1_out, adder_2_out, adder_3_out, adder_4_out, Address_Counter_A_q, counter_2_q,
       register_1_q, register_3_q;
  wire [7:0] counter_3_q;
  wire [63:0] core_8x8_1_r11, core_8x8_1_r12, core_8x8_1_r21, core_8x8_1_r22, ram_1_dout, ram_2_dout,
       ram_3_dout, ram_4_dout, ram_5_dout, ram_6_dout, ram_7_dout, ram_8_dout, ram_9_dout, ram_10_dout,
       ram_11_dout, ram_12_dout, ram_13_dout, ram_14_dout, ram_15_dout, ram_16_dout, ram_17_dout,
       ram_18_dout, ram_19_dout, ram_20_dout, ram_23_dout, ram_24_dout, ram_25_dout, ram_26_dout,
       ram_29_dout, ram_30_dout, ram_31_dout, ram_32_dout, ram_33_dout, ram_34_dout, ram_35_dout, ram_36_dout;

  ROM #(.dataWidth(64)) rom_1 ();  // open: addr, data
  and and_1 (and_1_out, Address_Counter_A_carry, counter_2_carry);
  Adder #(.width(4)) adder_1 (.a(register_1_q), .b(4'b0100), .out(adder_1_out));  // open: cin, cout
  Register #(.width(4)) register_1 (.D(adder_1_out), .en(and_1_out), .clk(clock_1_out), .Q(register_1_q));  // open: clr
  // Probe on adder_2_out
  Adder #(.width(4)) adder_2 (.a(Address_Counter_A_q), .b(register_1_q), .out(adder_2_out));  // open: cin, cout
  Counter #(.max('h3), .width(4)) Address_Counter_A (
    .count(counter_2_carry), .clk(clock_1_out), .carry(Address_Counter_A_carry), .Q(Address_Counter_A_q));  // open: clr, load, up, D
  RAM #(.addrWidth(4), .dataWidth(64), .\type ("nonvolatile")) ram_1 (
    .addr(adder_2_out), .oe(1'b1), .clk(clock_1_out), .dout(ram_1_dout));  // open: we, din
  RAM #(.addrWidth(4), .dataWidth(64), .\type ("nonvolatile")) ram_2 (
    .addr(adder_2_out), .oe(1'b1), .clk(clock_1_out), .dout(ram_2_dout));  // open: we, din
  RAM #(.addrWidth(4), .dataWidth(64), .\type ("nonvolatile")) ram_3 (
    .addr(adder_2_out), .oe(1'b1), .clk(clock_1_out), .dout(ram_3_dout));  // open: we, din
  RAM #(.addrWidth(4), .dataWidth(64), .\type ("nonvolatile")) ram_4 (
    .addr(adder_2_out), .oe(1'b1), .clk(clock_1_out), .dout(ram_4_dout));  // open: we, din
  Clock clock_1 (.out(clock_1_out));
  // Probe on ram_3_dout
  // Probe on ram_2_dout
  // Probe on ram_1_dout
  // Probe on ram_4_dout
  RAM #(.addrWidth(4), .dataWidth(64), .\type ("nonvolatile")) ram_5 (
    .addr(adder_2_out), .clk(clock_1_out), .dout(ram_5_dout));  // open: we, oe, din
  RAM #(.addrWidth(4), .dataWidth(64), .\type ("nonvolatile")) ram_6 (
    .addr(adder_2_out), .clk(clock_1_out), .dout(ram_6_dout));  // open: we, oe, din
  RAM #(.addrWidth(4), .dataWidth(64), .\type ("nonvolatile")) ram_7 (
    .addr(adder_2_out), .clk(clock_1_out), .dout(ram_7_dout));  // open: we, oe, din
  RAM #(.addrWidth(4), .dataWidth(64), .\type ("nonvolatile")) ram_8 (
    .addr(adder_2_out), .clk(clock_1_out), .dout(ram_8_dout));  // open: we, oe, din
  // Probe on ram_7_dout
  // Probe on ram_6_dout
  // Probe on ram_5_dout
  // Probe on ram_8_dout
  Counter #(.max('h0), .width(2)) counter_1 ();  // open: clr, load, up, count, clk, D, carry, Q
  RAM #(.addrWidth(4), .dataWidth(64), .\type ("nonvolatile")) ram_9 (
    .addr(adder_2_out), .clk(clock_1_out), .dout(ram_9_dout));  // open: we, oe, din
  RAM #(.addrWidth(4), .dataWidth(64), .\type ("nonvolatile")) ram_10 (
    .addr(adder_2_out), .clk(clock_1_out), .dout(ram_10_dout));  // open: we, oe, din
  RAM #(.addrWidth(4), .dataWidth(64), .\type ("nonvolatile")) ram_11 (
    .addr(adder_2_out), .clk(clock_1_out), .dout(ram_11_dout));  // open: we, oe, din
  RAM #(.addrWidth(4), .dataWidth(64), .\type ("nonvolatile")) ram_12 (
    .addr(adder_2_out), .clk(clock_1_out), .dout(ram_12_dout));  // open: we, oe, din
  // Probe on ram_11_dout
  // Probe on ram_10_dout
  // Probe on ram_9_dout
  // Probe on ram_12_dout
  RAM #(.addrWidth(4), .dataWidth(64), .\type ("nonvolatile")) ram_13 (
    .addr(adder_2_out), .clk(clock_1_out), .dout(ram_13_dout));  // open: we, oe, din
  RAM #(.addrWidth(4), .dataWidth(64), .\type ("nonvolatile")) ram_14 (
    .addr(adder_2_out), .clk(clock_1_out), .dout(ram_14_dout));  // open: we, oe, din
  RAM #(.addrWidth(4), .dataWidth(64), .\type ("nonvolatile")) ram_15 (
    .addr(adder_2_out), .clk(clock_1_out), .dout(ram_15_dout));  // open: we, oe, din
  RAM #(.addrWidth(4), .dataWidth(64), .\type ("nonvolatile")) ram_16 (
    .addr(adder_2_out), .clk(clock_1_out), .dout(ram_16_dout));  // open: we, oe, din
  // Probe on ram_13_dout
  // Probe on ram_16_dout
  // Probe on ram_15_dout
  // Probe on ram_14_dout
  Counter #(.max('h3), .width(4)) counter_2 (
    .clk(clock_1_out), .carry(counter_2_carry), .Q(counter_2_q));  // open: clr, load, up, count, D
  // Probe on core_8x8_1_r12
  // Probe on core_8x8_1_r21
  // Probe on core_8x8_1_r11
  // Probe on core_8x8_1_r22
  core_8x8 core_8x8_1 (
    .A11_11(ram_1_dout), .A11_12(ram_2_dout), .A11_21(ram_3_dout), .A11_22(ram_4_dout), .A12_11(ram_5_dout),
    .A12_12(ram_6_dout), .A12_21(ram_7_dout), .A12_22(ram_8_dout), .A13_11(ram_9_dout), .A13_12(ram_10_dout),
    .A13_21(ram_11_dout), .A13_22(ram_12_dout), .A14_11(ram_13_dout), .A14_12(ram_14_dout),
    .A14_21(ram_15_dout), .A14_22(ram_16_dout), .B11_11(ram_17_dout), .B11_12(ram_18_dout),
    .B11_21(ram_19_dout), .B11_22(ram_20_dout), .B21_11(ram_23_dout), .B21_12(ram_24_dout),
    .B21_21(ram_25_dout), .B21_22(ram_26_dout), .B31_11(ram_29_dout), .B31_12(ram_30_dout),
    .B31_21(ram_31_dout), .B31_22(ram_32_dout), .B41_11(ram_33_dout), .B41_12(ram_34_dout),
    .B41_21(ram_35_dout), .B41_22(ram_36_dout), .R11(core_8x8_1_r11), .R12(core_8x8_1_r12),
    .R21(core_8x8_1_r21), .R22(core_8x8_1_r22));
  RAM #(.addrWidth(4), .dataWidth(64), .\type ("nonvolatile")) ram_17 (
    .addr(adder_4_out), .oe(1'b1), .clk(clock_1_out), .dout(ram_17_dout));  // open: we, din
  RAM #(.addrWidth(4), .dataWidth(64), .\type ("nonvolatile")) ram_18 (
    .addr(adder_4_out), .oe(1'b1), .clk(clock_1_out), .dout(ram_18_dout));  // open: we, din
  RAM #(.addrWidth(4), .dataWidth(64), .\type ("nonvolatile")) ram_19 (
    .addr(adder_4_out), .oe(1'b1), .clk(clock_1_out), .dout(ram_19_dout));  // open: we, din
  RAM #(.addrWidth(4), .dataWidth(64), .\type ("nonvolatile")) ram_20 (
    .addr(adder_4_out), .oe(1'b1), .clk(clock_1_out), .dout(ram_20_dout));  // open: we, din
  Hex_Digit_Display hex_digit_display_1 ();  // open: value, dp
  and and_2 (and_2_out, Address_Counter_A_carry, counter_2_carry);
  Register #(.width(1)) register_2 (
    .D(clock_1_out), .en(clock_1_out), .clk(clock_1_out), .Q(register_2_q));  // open: clr
  Register #(.width(4)) register_3 (.D(adder_3_out), .en(and_2_out), .clk(clock_1_out), .Q(register_3_q));  // open: clr
  Adder #(.width(4)) adder_3 (.a(4'b0100), .b(register_3_q), .out(adder_3_out));  // open: cin, cout
  // Probe on ram_17_dout
  Counter counter_3 (.count(register_2_q), .clk(clock_1_out), .Q(counter_3_q));  // open: clr, load, up, D, carry
  // Probe on ram_20_dout
  // Probe on adder_4_out
  Adder #(.width(4)) adder_4 (.a(register_3_q), .b(counter_2_q), .out(adder_4_out));  // open: cin, cout
  // Probe on ram_18_dout
  // Probe on ram_19_dout
  RAM #(.dataWidth(64)) ram_21 (
    .addr(counter_3_q), .we(1'b1), .clk(clock_1_out), .din(core_8x8_1_r11));  // open: oe, dout
  RAM #(.dataWidth(64)) ram_22 (
    .addr(counter_3_q), .we(1'b1), .clk(clock_1_out), .din(core_8x8_1_r21));  // open: oe, dout
  RAM #(.addrWidth(4), .dataWidth(64), .\type ("nonvolatile")) ram_23 (
    .addr(adder_4_out), .clk(clock_1_out), .dout(ram_23_dout));  // open: we, oe, din
  RAM #(.addrWidth(4), .dataWidth(64), .\type ("nonvolatile")) ram_24 (
    .addr(adder_4_out), .clk(clock_1_out), .dout(ram_24_dout));  // open: we, oe, din
  RAM #(.addrWidth(4), .dataWidth(64), .\type ("nonvolatile")) ram_25 (
    .addr(adder_4_out), .clk(clock_1_out), .dout(ram_25_dout));  // open: we, oe, din
  RAM #(.addrWidth(4), .dataWidth(64), .\type ("nonvolatile")) ram_26 (
    .addr(adder_4_out), .clk(clock_1_out), .dout(ram_26_dout));  // open: we, oe, din
  // Probe on ram_24_dout
  // Probe on ram_23_dout
  RAM #(.dataWidth(64)) ram_27 (
    .addr(counter_3_q), .we(1'b1), .clk(clock_1_out), .din(core_8x8_1_r12));  // open: oe, dout
  RAM #(.dataWidth(64)) ram_28 (
    .addr(counter_3_q), .we(1'b1), .clk(clock_1_out), .din(core_8x8_1_r22));  // open: oe, dout
  // Probe on ram_25_dout
  // Probe on ram_26_dout
  RAM #(.addrWidth(4), .dataWidth(64), .\type ("nonvolatile")) ram_29 (
    .addr(adder_4_out), .clk(clock_1_out), .dout(ram_29_dout));  // open: we, oe, din
  RAM #(.addrWidth(4), .dataWidth(64), .\type ("nonvolatile")) ram_30 (
    .addr(adder_4_out), .clk(clock_1_out), .dout(ram_30_dout));  // open: we, oe, din
  RAM #(.addrWidth(4), .dataWidth(64), .\type ("nonvolatile")) ram_31 (
    .addr(adder_4_out), .clk(clock_1_out), .dout(ram_31_dout));  // open: we, oe, din
  RAM #(.addrWidth(4), .dataWidth(64), .\type ("nonvolatile")) ram_32 (
    .addr(adder_4_out), .clk(clock_1_out), .dout(ram_32_dout));  // open: we, oe, din
  // Probe on ram_29_dout
  // Probe on ram_30_dout
  // Probe on ram_32_dout
  // Probe on ram_31_dout
  RAM #(.addrWidth(4), .dataWidth(64), .\type ("nonvolatile")) ram_33 (
    .addr(adder_4_out), .clk(clock_1_out), .dout(ram_33_dout));  // open: we, oe, din
  RAM #(.addrWidth(4), .dataWidth(64), .\type ("nonvolatile")) ram_34 (
    .addr(adder_4_out), .clk(clock_1_out), .dout(ram_34_dout));  // open: we, oe, din
  RAM #(.addrWidth(4), .dataWidth(64), .\type ("nonvolatile")) ram_35 (
    .addr(adder_4_out), .clk(clock_1_out), .dout(ram_35_dout));  // open: we, oe, din
  RAM #(.addrWidth(4), .dataWidth(64), .\type ("nonvolatile")) ram_36 (
    .addr(adder_4_out), .clk(clock_1_out), .dout(ram_36_dout));  // open: we, oe, din
  // Probe on ram_33_dout
  // Probe on ram_35_dout
  // Probe on ram_34_dout
  // Probe on ram_36_dout

  // Notes on the sheet:
  //   A11
  //   A12
  //   A13
  //   A14
  //   B11
  //   B21
  //   B31
  //   B41
endmodule

module nextStuff (
  input  in_1
);

  wire Address_Counter_A_carry, and_1_out, and_2_out, clock_1_out, counter_2_carry, register_2_q;
  wire [3:0] adder_1_out, adder_2_out, adder_3_out, adder_4_out, Address_Counter_A_q, counter_2_q,
       instruction_splitter_1_opcode, register_1_q, register_3_q;
  wire [7:0] counter_1_q, counter_3_q, INST_MAR_q, instruction_splitter_1_address_a,
       instruction_splitter_1_address_b, MAR_A_q, MAR_B_q;
  wire [23:0] INST_MBR_q, INST_RAM_dout;
  wire [63:0] core_8x8_1_r11, core_8x8_1_r12, core_8x8_1_r21, core_8x8_1_r22, MBR_A_q, MBR_B_q, ram_1_dout,
       ram_2_dout, ram_3_dout, ram_4_dout, ram_5_dout, ram_6_dout, ram_7_dout, ram_8_dout, ram_9_dout,
       ram_10_dout, ram_11_dout, ram_12_dout, ram_13_dout, ram_14_dout, ram_15_dout, ram_16_dout,
       ram_17_dout, ram_18_dout, ram_19_dout, ram_20_dout, ram_23_dout, ram_24_dout, ram_25_dout,
       ram_26_dout, ram_29_dout, ram_30_dout, ram_31_dout, ram_32_dout, ram_33_dout, ram_34_dout,
       ram_35_dout, ram_36_dout, RAM_A_dout, RAM_B_dout;

  Counter counter_1 (.clk(clock_1_out), .Q(counter_1_q));  // open: clr, load, up, count, D, carry
  Register INST_MAR (.D(counter_1_q), .en(in_1), .clk(clock_1_out), .Q(INST_MAR_q));  // open: clr
  Adder #(.width(4)) adder_1 (.a(register_1_q), .b(4'b0100), .out(adder_1_out));  // open: cin, cout
  and and_1 (and_1_out, Address_Counter_A_carry, counter_2_carry);
  Register #(.width(4)) register_1 (.D(adder_1_out), .en(and_1_out), .clk(clock_1_out), .Q(register_1_q));  // open: clr
  // Probe on adder_2_out
  Adder #(.width(4)) adder_2 (.a(Address_Counter_A_q), .b(register_1_q), .out(adder_2_out));  // open: cin, cout
  RAM #(.dataWidth(24), .\type ("nonvolatile")) INST_RAM (
    .addr(INST_MAR_q), .dout(INST_RAM_dout));  // open: we, oe, clk, din
  Counter #(.max('h3), .width(4)) Address_Counter_A (
    .count(counter_2_carry), .clk(clock_1_out), .carry(Address_Counter_A_carry), .Q(Address_Counter_A_q));  // open: clr, load, up, D
  Register #(.width(24)) INST_MBR (.D(INST_RAM_dout), .Q(INST_MBR_q));  // open: en, clk, clr
  RAM #(.addrWidth(4), .dataWidth(64), .\type ("nonvolatile")) ram_1 (
    .addr(adder_2_out), .oe(1'b1), .clk(clock_1_out), .dout(ram_1_dout));  // open: we, din
  RAM #(.addrWidth(4), .dataWidth(64), .\type ("nonvolatile")) ram_2 (
    .addr(adder_2_out), .oe(1'b1), .clk(clock_1_out), .dout(ram_2_dout));  // open: we, din
  RAM #(.addrWidth(4), .dataWidth(64), .\type ("nonvolatile")) ram_3 (
    .addr(adder_2_out), .oe(1'b1), .clk(clock_1_out), .dout(ram_3_dout));  // open: we, din
  RAM #(.addrWidth(4), .dataWidth(64), .\type ("nonvolatile")) ram_4 (
    .addr(adder_2_out), .oe(1'b1), .clk(clock_1_out), .dout(ram_4_dout));  // open: we, din
  Clock clock_1 (.out(clock_1_out));
  // Probe on ram_3_dout
  // Probe on ram_2_dout
  // Probe on ram_1_dout
  instruction_splitter instruction_splitter_1 (
    .instruction(INST_MBR_q), .opcode(instruction_splitter_1_opcode),
    .address_A(instruction_splitter_1_address_a), .address_B(instruction_splitter_1_address_b));  // open: WE, CLOCK, flag
  // Probe on ram_4_dout
  RAM #(.addrWidth(4), .dataWidth(64), .\type ("nonvolatile")) ram_5 (
    .addr(adder_2_out), .clk(clock_1_out), .dout(ram_5_dout));  // open: we, oe, din
  RAM #(.addrWidth(4), .dataWidth(64), .\type ("nonvolatile")) ram_6 (
    .addr(adder_2_out), .clk(clock_1_out), .dout(ram_6_dout));  // open: we, oe, din
  RAM #(.addrWidth(4), .dataWidth(64), .\type ("nonvolatile")) ram_7 (
    .addr(adder_2_out), .clk(clock_1_out), .dout(ram_7_dout));  // open: we, oe, din
  RAM #(.addrWidth(4), .dataWidth(64), .\type ("nonvolatile")) ram_8 (
    .addr(adder_2_out), .clk(clock_1_out), .dout(ram_8_dout));  // open: we, oe, din
  Register MAR_A (.D(instruction_splitter_1_address_a), .Q(MAR_A_q));  // open: en, clk, clr
  Register MAR_B (.D(instruction_splitter_1_address_b), .Q(MAR_B_q));  // open: en, clk, clr
  // Probe on ram_7_dout
  // Probe on ram_6_dout
  // Probe on ram_5_dout
  // Probe on ram_8_dout
  RAM #(.dataWidth(64), .\type ("nonvolatile")) RAM_A (.addr(MAR_A_q), .dout(RAM_A_dout));  // open: we, oe, clk, din
  RAM #(.dataWidth(64), .\type ("nonvolatile")) RAM_B (.addr(MAR_B_q), .dout(RAM_B_dout));  // open: we, oe, clk, din
  RAM #(.addrWidth(4), .dataWidth(64), .\type ("nonvolatile")) ram_9 (
    .addr(adder_2_out), .clk(clock_1_out), .dout(ram_9_dout));  // open: we, oe, din
  RAM #(.addrWidth(4), .dataWidth(64), .\type ("nonvolatile")) ram_10 (
    .addr(adder_2_out), .clk(clock_1_out), .dout(ram_10_dout));  // open: we, oe, din
  RAM #(.addrWidth(4), .dataWidth(64), .\type ("nonvolatile")) ram_11 (
    .addr(adder_2_out), .clk(clock_1_out), .dout(ram_11_dout));  // open: we, oe, din
  RAM #(.addrWidth(4), .dataWidth(64), .\type ("nonvolatile")) ram_12 (
    .addr(adder_2_out), .clk(clock_1_out), .dout(ram_12_dout));  // open: we, oe, din
  Register #(.width(64)) MBR_A (.D(RAM_A_dout), .Q(MBR_A_q));  // open: en, clk, clr
  // Probe on ram_10_dout
  // Probe on ram_9_dout
  Register #(.width(64)) MBR_B (.D(RAM_B_dout), .Q(MBR_B_q));  // open: en, clk, clr
  // Probe on ram_12_dout
  // Probe on ram_11_dout
  RAM #(.addrWidth(4), .dataWidth(64), .\type ("nonvolatile")) ram_13 (
    .addr(adder_2_out), .clk(clock_1_out), .dout(ram_13_dout));  // open: we, oe, din
  RAM #(.addrWidth(4), .dataWidth(64), .\type ("nonvolatile")) ram_14 (
    .addr(adder_2_out), .clk(clock_1_out), .dout(ram_14_dout));  // open: we, oe, din
  RAM #(.addrWidth(4), .dataWidth(64), .\type ("nonvolatile")) ram_15 (
    .addr(adder_2_out), .clk(clock_1_out), .dout(ram_15_dout));  // open: we, oe, din
  RAM #(.addrWidth(4), .dataWidth(64), .\type ("nonvolatile")) ram_16 (
    .addr(adder_2_out), .clk(clock_1_out), .dout(ram_16_dout));  // open: we, oe, din
  // Probe on ram_14_dout
  // Probe on ram_13_dout
  // Probe on ram_16_dout
  // Probe on ram_15_dout
  Counter #(.max('h3), .width(4)) counter_2 (
    .clk(clock_1_out), .carry(counter_2_carry), .Q(counter_2_q));  // open: clr, load, up, count, D
  // Probe on core_8x8_1_r11
  // Probe on core_8x8_1_r12
  // Probe on core_8x8_1_r21
  // Probe on core_8x8_1_r22
  core_8x8 core_8x8_1 (
    .A11_11(ram_1_dout), .A11_12(ram_2_dout), .A11_21(ram_3_dout), .A11_22(ram_4_dout), .A12_11(ram_5_dout),
    .A12_12(ram_6_dout), .A12_21(ram_7_dout), .A12_22(ram_8_dout), .A13_11(ram_9_dout), .A13_12(ram_10_dout),
    .A13_21(ram_11_dout), .A13_22(ram_12_dout), .A14_11(ram_13_dout), .A14_12(ram_14_dout),
    .A14_21(ram_15_dout), .A14_22(ram_16_dout), .B11_11(ram_17_dout), .B11_12(ram_18_dout),
    .B11_21(ram_19_dout), .B11_22(ram_20_dout), .B21_11(ram_23_dout), .B21_12(ram_24_dout),
    .B21_21(ram_25_dout), .B21_22(ram_26_dout), .B31_11(ram_29_dout), .B31_12(ram_30_dout),
    .B31_21(ram_31_dout), .B31_22(ram_32_dout), .B41_11(ram_33_dout), .B41_12(ram_34_dout),
    .B41_21(ram_35_dout), .B41_22(ram_36_dout), .R11(core_8x8_1_r11), .R12(core_8x8_1_r12),
    .R21(core_8x8_1_r21), .R22(core_8x8_1_r22));
  RAM #(.addrWidth(4), .dataWidth(64), .\type ("nonvolatile")) ram_17 (
    .addr(adder_4_out), .oe(1'b1), .clk(clock_1_out), .dout(ram_17_dout));  // open: we, din
  RAM #(.addrWidth(4), .dataWidth(64), .\type ("nonvolatile")) ram_18 (
    .addr(adder_4_out), .oe(1'b1), .clk(clock_1_out), .dout(ram_18_dout));  // open: we, din
  RAM #(.addrWidth(4), .dataWidth(64), .\type ("nonvolatile")) ram_19 (
    .addr(adder_4_out), .oe(1'b1), .clk(clock_1_out), .dout(ram_19_dout));  // open: we, din
  RAM #(.addrWidth(4), .dataWidth(64), .\type ("nonvolatile")) ram_20 (
    .addr(adder_4_out), .oe(1'b1), .clk(clock_1_out), .dout(ram_20_dout));  // open: we, din
  Hex_Digit_Display hex_digit_display_1 ();  // open: value, dp
  and and_2 (and_2_out, Address_Counter_A_carry, counter_2_carry);
  Register #(.width(1)) register_2 (
    .D(clock_1_out), .en(clock_1_out), .clk(clock_1_out), .Q(register_2_q));  // open: clr
  Register #(.width(4)) register_3 (.D(adder_3_out), .en(and_2_out), .clk(clock_1_out), .Q(register_3_q));  // open: clr
  Adder #(.width(4)) adder_3 (.a(4'b0100), .b(register_3_q), .out(adder_3_out));  // open: cin, cout
  // Probe on ram_17_dout
  Counter counter_3 (.count(register_2_q), .clk(clock_1_out), .Q(counter_3_q));  // open: clr, load, up, D, carry
  // Probe on ram_20_dout
  RAM #(.dataWidth(64)) ram_21 (
    .addr(counter_3_q), .we(1'b1), .clk(clock_1_out), .din(core_8x8_1_r11));  // open: oe, dout
  RAM #(.dataWidth(64)) ram_22 (
    .addr(counter_3_q), .we(1'b1), .clk(clock_1_out), .din(core_8x8_1_r21));  // open: oe, dout
  // Probe on adder_4_out
  Adder #(.width(4)) adder_4 (.a(register_3_q), .b(counter_2_q), .out(adder_4_out));  // open: cin, cout
  // Probe on ram_18_dout
  // Probe on ram_19_dout
  RAM #(.addrWidth(4), .dataWidth(64), .\type ("nonvolatile")) ram_23 (
    .addr(adder_4_out), .clk(clock_1_out), .dout(ram_23_dout));  // open: we, oe, din
  RAM #(.addrWidth(4), .dataWidth(64), .\type ("nonvolatile")) ram_24 (
    .addr(adder_4_out), .clk(clock_1_out), .dout(ram_24_dout));  // open: we, oe, din
  RAM #(.addrWidth(4), .dataWidth(64), .\type ("nonvolatile")) ram_25 (
    .addr(adder_4_out), .clk(clock_1_out), .dout(ram_25_dout));  // open: we, oe, din
  RAM #(.addrWidth(4), .dataWidth(64), .\type ("nonvolatile")) ram_26 (
    .addr(adder_4_out), .clk(clock_1_out), .dout(ram_26_dout));  // open: we, oe, din
  // Probe on ram_24_dout
  // Probe on ram_23_dout
  RAM #(.dataWidth(64)) ram_27 (
    .addr(counter_3_q), .we(1'b1), .clk(clock_1_out), .din(core_8x8_1_r12));  // open: oe, dout
  RAM #(.dataWidth(64)) ram_28 (
    .addr(counter_3_q), .we(1'b1), .clk(clock_1_out), .din(core_8x8_1_r22));  // open: oe, dout
  // Probe on ram_25_dout
  // Probe on ram_26_dout
  RAM #(.addrWidth(4), .dataWidth(64), .\type ("nonvolatile")) ram_29 (
    .addr(adder_4_out), .clk(clock_1_out), .dout(ram_29_dout));  // open: we, oe, din
  RAM #(.addrWidth(4), .dataWidth(64), .\type ("nonvolatile")) ram_30 (
    .addr(adder_4_out), .clk(clock_1_out), .dout(ram_30_dout));  // open: we, oe, din
  RAM #(.addrWidth(4), .dataWidth(64), .\type ("nonvolatile")) ram_31 (
    .addr(adder_4_out), .clk(clock_1_out), .dout(ram_31_dout));  // open: we, oe, din
  RAM #(.addrWidth(4), .dataWidth(64), .\type ("nonvolatile")) ram_32 (
    .addr(adder_4_out), .clk(clock_1_out), .dout(ram_32_dout));  // open: we, oe, din
  // Probe on ram_30_dout
  // Probe on ram_29_dout
  // Probe on ram_32_dout
  // Probe on ram_31_dout
  RAM #(.addrWidth(4), .dataWidth(64), .\type ("nonvolatile")) ram_33 (
    .addr(adder_4_out), .clk(clock_1_out), .dout(ram_33_dout));  // open: we, oe, din
  RAM #(.addrWidth(4), .dataWidth(64), .\type ("nonvolatile")) ram_34 (
    .addr(adder_4_out), .clk(clock_1_out), .dout(ram_34_dout));  // open: we, oe, din
  RAM #(.addrWidth(4), .dataWidth(64), .\type ("nonvolatile")) ram_35 (
    .addr(adder_4_out), .clk(clock_1_out), .dout(ram_35_dout));  // open: we, oe, din
  RAM #(.addrWidth(4), .dataWidth(64), .\type ("nonvolatile")) ram_36 (
    .addr(adder_4_out), .clk(clock_1_out), .dout(ram_36_dout));  // open: we, oe, din
  // Probe on ram_34_dout
  // Probe on ram_33_dout
  // Probe on ram_35_dout
  // Probe on ram_36_dout

  // Notes on the sheet:
  //   A11
  //   A12
  //   A13
  //   A14
  //   B11
  //   B21
  //   B31
  //   B41
endmodule

module instruction_splitter (
  input  WE,
  input  CLOCK,
  input  [23:0] instruction,
  output [3:0] flag,
  output [3:0] opcode,
  output [7:0] address_A,
  output [7:0] address_B
);

  Register #(.width(24)) register_1 (
    .D(instruction), .en(WE), .clk(CLOCK), .Q({address_B, address_A, opcode, flag}));  // open: clr
endmodule
